// Logisim project ARITMÉTICA_.circ as structural Verilog
module SOMADOR (
  input  VEM_1,
  input  A,
  input  B,
  output SOMA,
  output VAI_1
);

  wire and_1_out, and_2_out, and_3_out, and_4_out, and_5_out, and_6_out, and_7_out;

  and and_1 (and_1_out, VEM_1, ~A, ~B);  // AND_Gate
  and and_2 (and_2_out, B, A, VEM_1);
  and and_3 (and_3_out, ~VEM_1, A, ~B);  // AND_Gate
  and and_4 (and_4_out, ~VEM_1, ~A, B);  // AND_Gate
  and and_5 (and_5_out, VEM_1, B);
  and and_6 (and_6_out, VEM_1, A);
  and and_7 (and_7_out, A, B);
  or or_1 (SOMA, and_1_out, and_2_out, and_3_out, and_4_out);
  or or_2 (VAI_1, and_5_out, and_6_out, and_7_out);
endmodule

module SUBTRATOR (
  input  VEM_1,
  input  A,
  input  B,
  output \SUBTRAÇÃO ,
  output VAI_1
);

  wire and_1_out, and_2_out, and_3_out, and_4_out, and_5_out, and_6_out, and_7_out;

  and and_1 (and_1_out, A, ~B, ~VEM_1);  // AND_Gate
  and and_2 (and_2_out, A, B, VEM_1);
  and and_3 (and_3_out, ~A, B, ~VEM_1);  // AND_Gate
  and and_4 (and_4_out, ~A, ~B, VEM_1);  // AND_Gate
  and and_5 (and_5_out, A, ~VEM_1);  // AND_Gate
  and and_6 (and_6_out, B, ~VEM_1);  // AND_Gate
  and and_7 (and_7_out, A, B);
  or or_1 (\SUBTRAÇÃO , and_1_out, and_2_out, and_3_out, and_4_out);
  or or_2 (VAI_1, and_5_out, and_6_out, and_7_out);
endmodule

module MULTIPLICADOR (
  input  VEM_1,
  input  A,
  input  B,
  output \MULTIPLICAÇÃO ,
  output VAI_1
);

  wire and_1_out, and_2_out, and_3_out;

  and and_1 (and_1_out, ~B, VEM_1);  // AND_Gate
  and and_2 (and_2_out, A, B, ~VEM_1);  // AND_Gate
  and and_3 (and_3_out, ~A, VEM_1);  // AND_Gate
  and and_4 (VAI_1, B, A, VEM_1);
  or or_1 (\MULTIPLICAÇÃO , and_1_out, and_2_out, and_3_out);
endmodule
