// Logisim project ARITMÉTICA_32_BITS.circ as structural Verilog: 2 circuits, main circuit main
module main (
  input  [31:0] in_1,
  input  [31:0] in_2
);

  SOMADOR_32BITS somador_32bits_1 ();  // open: S31, S30, A31, A30, S29, A29, A28, A27, S28, A26, A25, A24, A23, S27, A22, A21, A20, S26, A19, A18, A17, A16, S25, A15, A14, A13, S24, A12, A11, A10, A9, S23, A8, A7, A6, S22, A5, A4, A3, A2, S21, A1, A0, S20, S19, S18, B31, B30, B29, S17, B28, B27, B26, B25, S16, B24, B23, B22, S15, B21, B20, B19, B18, S14, B17, B16, B15, S13, B14, B13, B12, B11, S12, B10, B9, B8, S11, B7, B6, B5, B4, S10, B3, B2, B1, S9, B0, S8, S7, S6, S5, S4, S3, S2, S1, S0, OVERFLOW
endmodule

// GSOMA32
module SOMADOR_32BITS (
  input  A31,
  input  A30,
  input  A29,
  input  A28,
  input  A27,
  input  A26,
  input  A25,
  input  A24,
  input  A23,
  input  A22,
  input  A21,
  input  A20,
  input  A19,
  input  A18,
  input  A17,
  input  A16,
  input  A15,
  input  A14,
  input  A13,
  input  A12,
  input  A11,
  input  A10,
  input  A9,
  input  A8,
  input  A7,
  input  A6,
  input  A5,
  input  A4,
  input  A3,
  input  A2,
  input  A1,
  input  A0,
  input  B31,
  input  B30,
  input  B29,
  input  B28,
  input  B27,
  input  B26,
  input  B25,
  input  B24,
  input  B23,
  input  B22,
  input  B21,
  input  B20,
  input  B19,
  input  B18,
  input  B17,
  input  B16,
  input  B15,
  input  B14,
  input  B13,
  input  B12,
  input  B11,
  input  B10,
  input  B9,
  input  B8,
  input  B7,
  input  B6,
  input  B5,
  input  B4,
  input  B3,
  input  B2,
  input  B1,
  input  B0,
  output OVERFLOW,
  output S31,
  output S30,
  output S29,
  output S28,
  output S27,
  output S26,
  output S25,
  output S24,
  output S23,
  output S22,
  output S21,
  output S20,
  output S19,
  output S18,
  output S17,
  output S16,
  output S15,
  output S14,
  output S13,
  output S12,
  output S11,
  output S10,
  output S9,
  output S8,
  output S7,
  output S6,
  output S5,
  output S4,
  output S3,
  output S2,
  output S1,
  output S0
);

  wire somador_2_vai_1, somador_3_vai_1, somador_4_vai_1, somador_5_vai_1, somador_6_vai_1, somador_7_vai_1,
       somador_8_vai_1, somador_9_vai_1, somador_10_vai_1, somador_11_vai_1, somador_12_vai_1,
       somador_13_vai_1, somador_14_vai_1, somador_15_vai_1, somador_16_vai_1, somador_17_vai_1,
       somador_18_vai_1, somador_19_vai_1, somador_20_vai_1, somador_21_vai_1, somador_22_vai_1,
       somador_23_vai_1, somador_24_vai_1, somador_25_vai_1, somador_26_vai_1, somador_27_vai_1,
       somador_28_vai_1, somador_29_vai_1, somador_30_vai_1, somador_31_vai_1, somador_32_vai_1;

  SOMADOR somador_1 (.VEM_1(somador_2_vai_1), .A(A31), .B(B31), .SOMA(S31), .VAI_1(OVERFLOW));
  SOMADOR somador_2 (.VEM_1(somador_3_vai_1), .A(A30), .B(B30), .SOMA(S30), .VAI_1(somador_2_vai_1));
  SOMADOR somador_3 (.VEM_1(somador_4_vai_1), .A(A29), .B(B29), .SOMA(S29), .VAI_1(somador_3_vai_1));
  SOMADOR somador_4 (.VEM_1(somador_5_vai_1), .A(A28), .B(B28), .SOMA(S28), .VAI_1(somador_4_vai_1));
  SOMADOR somador_5 (.VEM_1(somador_6_vai_1), .A(A27), .B(B27), .SOMA(S27), .VAI_1(somador_5_vai_1));
  SOMADOR somador_6 (.VEM_1(somador_8_vai_1), .A(A26), .B(B26), .SOMA(S26), .VAI_1(somador_6_vai_1));
  SOMADOR somador_7 (.VEM_1(somador_9_vai_1), .A(A24), .B(B24), .SOMA(S24), .VAI_1(somador_7_vai_1));
  SOMADOR somador_8 (.VEM_1(somador_7_vai_1), .A(A25), .B(B25), .SOMA(S25), .VAI_1(somador_8_vai_1));
  SOMADOR somador_9 (.VEM_1(somador_10_vai_1), .A(A23), .B(B23), .SOMA(S23), .VAI_1(somador_9_vai_1));
  SOMADOR somador_10 (.VEM_1(somador_11_vai_1), .A(A22), .B(B22), .SOMA(S22), .VAI_1(somador_10_vai_1));
  SOMADOR somador_11 (.VEM_1(somador_12_vai_1), .A(A21), .B(B21), .SOMA(S21), .VAI_1(somador_11_vai_1));
  SOMADOR somador_12 (.VEM_1(somador_13_vai_1), .A(A20), .B(B20), .SOMA(S20), .VAI_1(somador_12_vai_1));
  SOMADOR somador_13 (.VEM_1(somador_14_vai_1), .A(A19), .B(B19), .SOMA(S19), .VAI_1(somador_13_vai_1));
  SOMADOR somador_14 (.VEM_1(somador_16_vai_1), .A(A18), .B(B18), .SOMA(S18), .VAI_1(somador_14_vai_1));
  SOMADOR somador_15 (.VEM_1(somador_17_vai_1), .A(A16), .B(B16), .SOMA(S16), .VAI_1(somador_15_vai_1));
  SOMADOR somador_16 (.VEM_1(somador_15_vai_1), .A(A17), .B(B17), .SOMA(S17), .VAI_1(somador_16_vai_1));
  SOMADOR somador_17 (.VEM_1(somador_18_vai_1), .A(A15), .B(B15), .SOMA(S15), .VAI_1(somador_17_vai_1));
  SOMADOR somador_18 (.VEM_1(somador_19_vai_1), .A(A14), .B(B14), .SOMA(S14), .VAI_1(somador_18_vai_1));
  SOMADOR somador_19 (.VEM_1(somador_20_vai_1), .A(A13), .B(B13), .SOMA(S13), .VAI_1(somador_19_vai_1));
  SOMADOR somador_20 (.VEM_1(somador_21_vai_1), .A(A12), .B(B12), .SOMA(S12), .VAI_1(somador_20_vai_1));
  SOMADOR somador_21 (.VEM_1(somador_22_vai_1), .A(A11), .B(B11), .SOMA(S11), .VAI_1(somador_21_vai_1));
  SOMADOR somador_22 (.VEM_1(somador_24_vai_1), .A(A10), .B(B10), .SOMA(S10), .VAI_1(somador_22_vai_1));
  SOMADOR somador_23 (.VEM_1(somador_25_vai_1), .A(A8), .B(B8), .SOMA(S8), .VAI_1(somador_23_vai_1));
  SOMADOR somador_24 (.VEM_1(somador_23_vai_1), .A(A9), .B(B9), .SOMA(S9), .VAI_1(somador_24_vai_1));
  SOMADOR somador_25 (.VEM_1(somador_26_vai_1), .A(A7), .B(B7), .SOMA(S7), .VAI_1(somador_25_vai_1));
  SOMADOR somador_26 (.VEM_1(somador_27_vai_1), .A(A6), .B(B6), .SOMA(S6), .VAI_1(somador_26_vai_1));
  SOMADOR somador_27 (.VEM_1(somador_28_vai_1), .A(A5), .B(B5), .SOMA(S5), .VAI_1(somador_27_vai_1));
  SOMADOR somador_28 (.VEM_1(somador_29_vai_1), .A(A4), .B(B4), .SOMA(S4), .VAI_1(somador_28_vai_1));
  SOMADOR somador_29 (.VEM_1(somador_30_vai_1), .A(A3), .B(B3), .SOMA(S3), .VAI_1(somador_29_vai_1));
  SOMADOR somador_30 (.VEM_1(somador_31_vai_1), .A(A2), .B(B2), .SOMA(S2), .VAI_1(somador_30_vai_1));
  SOMADOR somador_31 (.VEM_1(somador_32_vai_1), .A(A1), .B(B1), .SOMA(S1), .VAI_1(somador_31_vai_1));
  SOMADOR somador_32 (.VEM_1(1'b0), .A(A0), .B(B0), .SOMA(S0), .VAI_1(somador_32_vai_1));
endmodule
