// Logisim project ARITMÉTICA_CORRIGIDO.circ as structural Verilog
module SOMADOR (
  input  VEM_1,
  input  A,
  input  B,
  output SOMA,
  output VAI_1
);

  wire and_1_out, and_2_out, and_3_out, xor_1_out;

  xor xor_1 (xor_1_out, B, A);
  and and_1 (and_1_out, B, VEM_1);
  and and_2 (and_2_out, A, VEM_1);
  and and_3 (and_3_out, A, B);
  xor xor_2 (SOMA, xor_1_out, VEM_1);
  or or_1 (VAI_1, and_1_out, and_2_out, and_3_out);
endmodule

module SUBTRATOR (
  input  VEM_1,
  input  A,
  input  B,
  output \SUBTRAÇÃO ,
  output VAI_1
);

  wire and_1_out, and_2_out, and_3_out, xor_1_out;

  xor xor_1 (xor_1_out, A, B);
  and and_1 (and_1_out, ~A, VEM_1);  // AND_Gate
  and and_2 (and_2_out, ~A, B);  // AND_Gate
  and and_3 (and_3_out, B, VEM_1);
  xor xor_2 (\SUBTRAÇÃO , xor_1_out, VEM_1);
  or or_1 (VAI_1, and_1_out, and_2_out, and_3_out);
endmodule

module MULTIPLICADOR (
  input  VEM_1,
  input  A,
  input  B,
  output \MULTIPLICAÇÃO ,
  output VAI_1
);

  wire and_1_out, and_2_out, and_3_out;

  and and_1 (and_1_out, ~B, VEM_1);  // AND_Gate
  and and_2 (and_2_out, A, B, ~VEM_1);  // AND_Gate
  and and_3 (and_3_out, ~A, VEM_1);  // AND_Gate
  and and_4 (VAI_1, B, A, VEM_1);
  or or_1 (\MULTIPLICAÇÃO , and_1_out, and_2_out, and_3_out);
endmodule
