// Logisim project SOMADORES.circ as structural Verilog: 5 circuits, main circuit main
module main (
);


  // Notes on the sheet:
  //   SOMA = VEM1 XOR A XOR B
  //   VAI 1 = (VEM1 AND B) OR (VEM1 AND A) OR (A AND B) 
endmodule

module somador_1bit (
  input  A,
  input  B,
  output SOMA,
  output VAI_1
);

  xor xor_1 (SOMA, B, A);
  and and_1 (VAI_1, B, A);
endmodule

module somador_4bit (
  input  [3:0] A,
  input  [3:0] B,
  output [3:0] out_3,
  output OVERFLOW
);

  wire somador_1bit_1_vai_1, somador_completo_2_bits_2_vai_1, somador_completo_2_bits_3_vai_1;

  somador_completo_2_bits somador_completo_2_bits_1 (
    .VEM_1(somador_completo_2_bits_2_vai_1), .A(A[3]), .B(B[3]), .SOMA(out_3[3]), .VAI_1(OVERFLOW));
  somador_completo_2_bits somador_completo_2_bits_2 (
    .VEM_1(somador_completo_2_bits_3_vai_1), .A(A[2]), .B(B[2]), .SOMA(out_3[2]),
    .VAI_1(somador_completo_2_bits_2_vai_1));
  somador_completo_2_bits somador_completo_2_bits_3 (
    .VEM_1(somador_1bit_1_vai_1), .A(A[1]), .B(B[1]), .SOMA(out_3[1]), .VAI_1(somador_completo_2_bits_3_vai_1));
  somador_1bit somador_1bit_1 (.A(A[0]), .B(B[0]), .SOMA(out_3[0]), .VAI_1(somador_1bit_1_vai_1));
endmodule

module somador_completo_2_bits (
  input  VEM_1,
  input  A,
  input  B,
  output SOMA,
  output VAI_1
);

  wire and_1_out, and_2_out, and_3_out, and_4_out, and_5_out, and_6_out, and_7_out;

  and and_1 (and_1_out, VEM_1, ~A, ~B);  // AND_Gate
  and and_2 (and_2_out, B, A, VEM_1);
  and and_3 (and_3_out, ~VEM_1, A, ~B);  // AND_Gate
  and and_4 (and_4_out, ~VEM_1, ~A, B);  // AND_Gate
  and and_5 (and_5_out, VEM_1, B);
  and and_6 (and_6_out, VEM_1, A);
  and and_7 (and_7_out, A, B);
  or or_1 (SOMA, and_1_out, and_2_out, and_3_out, and_4_out);
  or or_2 (VAI_1, and_5_out, and_6_out, and_7_out);
endmodule

module somador_completo_4_bits (
  input  A3,
  input  A2,
  input  A1,
  input  A0,
  input  B3,
  input  B2,
  input  B1,
  input  B0,
  output S3,
  output S2,
  output S1,
  output S0,
  output VAI_1
);

  wire somador_1bit_1_vai_1, somador_completo_2_bits_2_vai_1, somador_completo_2_bits_3_vai_1;

  somador_completo_2_bits somador_completo_2_bits_1 (
    .VEM_1(somador_completo_2_bits_2_vai_1), .A(A3), .B(B3), .SOMA(S3), .VAI_1(VAI_1));
  somador_completo_2_bits somador_completo_2_bits_2 (
    .VEM_1(somador_completo_2_bits_3_vai_1), .A(A2), .B(B2), .SOMA(S2),
    .VAI_1(somador_completo_2_bits_2_vai_1));
  somador_completo_2_bits somador_completo_2_bits_3 (
    .VEM_1(somador_1bit_1_vai_1), .A(A1), .B(B1), .SOMA(S1), .VAI_1(somador_completo_2_bits_3_vai_1));
  somador_1bit somador_1bit_1 (.A(A0), .B(B0), .SOMA(S0), .VAI_1(somador_1bit_1_vai_1));

  // Notes on the sheet:
  //   A
  //   B
  //   SOMA
endmodule
