// Logisim project SOMADOR_16BIT.circ as structural Verilog
module main (
);


  // Notes on the sheet:
  //   SOMA = VEM1 XOR A XOR B
  //   VAI 1 = (VEM1 AND B) OR (VEM1 AND A) OR (A AND B) 
endmodule

module somador_1bit (
  input  A,
  input  B,
  output SOMA,
  output VAI_1
);

  xor xor_1 (SOMA, B, A);
  and and_1 (VAI_1, B, A);
endmodule

module somador_4bit (
  input  [3:0] A,
  input  [3:0] B,
  output [3:0] out_3,
  output OVERFLOW
);

  wire somador_1bit_1_vai_1, somador_completo_2_bits_2_vai_1, somador_completo_2_bits_3_vai_1;

  somador_completo_2_bits somador_completo_2_bits_1 (
    .VEM_1(somador_completo_2_bits_2_vai_1), .A(A[3]), .B(B[3]), .SOMA(out_3[3]), .VAI_1(OVERFLOW));
  somador_completo_2_bits somador_completo_2_bits_2 (
    .VEM_1(somador_completo_2_bits_3_vai_1), .A(A[2]), .B(B[2]), .SOMA(out_3[2]),
    .VAI_1(somador_completo_2_bits_2_vai_1));
  somador_completo_2_bits somador_completo_2_bits_3 (
    .VEM_1(somador_1bit_1_vai_1), .A(A[1]), .B(B[1]), .SOMA(out_3[1]), .VAI_1(somador_completo_2_bits_3_vai_1));
  somador_1bit somador_1bit_1 (.A(A[0]), .B(B[0]), .SOMA(out_3[0]), .VAI_1(somador_1bit_1_vai_1));
endmodule

module somador_completo_2_bits (
  input  VEM_1,
  input  A,
  input  B,
  output SOMA,
  output VAI_1
);

  wire and_1_out, and_2_out, and_3_out, and_4_out, and_5_out, and_6_out, and_7_out;

  and and_1 (and_1_out, VEM_1, ~A, ~B);  // AND_Gate
  and and_2 (and_2_out, B, A, VEM_1);
  and and_3 (and_3_out, ~VEM_1, A, ~B);  // AND_Gate
  and and_4 (and_4_out, ~VEM_1, ~A, B);  // AND_Gate
  and and_5 (and_5_out, VEM_1, B);
  and and_6 (and_6_out, VEM_1, A);
  and and_7 (and_7_out, A, B);
  or or_1 (SOMA, and_1_out, and_2_out, and_3_out, and_4_out);
  or or_2 (VAI_1, and_5_out, and_6_out, and_7_out);
endmodule

module somador_completo_4_bits (
  input  A3,
  input  A2,
  input  A1,
  input  A0,
  input  B3,
  input  B2,
  input  B1,
  input  B0,
  output S3,
  output S2,
  output S1,
  output S0,
  output VAI1
);

  wire somador_completo_2_bits_2_vai_1, somador_completo_2_bits_3_vai_1, somador_completo_2_bits_4_vai_1;

  somador_completo_2_bits somador_completo_2_bits_1 (
    .VEM_1(somador_completo_2_bits_2_vai_1), .A(A3), .B(B3), .SOMA(S3), .VAI_1(VAI1));
  somador_completo_2_bits somador_completo_2_bits_2 (
    .VEM_1(somador_completo_2_bits_3_vai_1), .A(A2), .B(B2), .SOMA(S2),
    .VAI_1(somador_completo_2_bits_2_vai_1));
  somador_completo_2_bits somador_completo_2_bits_3 (
    .VEM_1(somador_completo_2_bits_4_vai_1), .A(A1), .B(B1), .SOMA(S1),
    .VAI_1(somador_completo_2_bits_3_vai_1));
  somador_completo_2_bits somador_completo_2_bits_4 (
    .VEM_1(1'b0), .A(A0), .B(B0), .SOMA(S0), .VAI_1(somador_completo_2_bits_4_vai_1));

  // Notes on the sheet:
  //   A
  //   B
  //   SOMA
endmodule

module SOMADOR_16_BITS (
  input  B15,
  input  B14,
  input  B13,
  input  B12,
  input  B11,
  input  B10,
  input  B9,
  input  B8,
  input  B7,
  input  B6,
  input  B5,
  input  B4,
  input  B3,
  input  B2,
  input  B1,
  input  B0,
  input  A0,
  input  A1,
  input  A2,
  input  A3,
  input  A4,
  input  A5,
  input  A6,
  input  A7,
  input  A8,
  input  A9,
  input  A10,
  input  A11,
  input  A12,
  input  A13,
  input  A14,
  input  A15,
  input  VEM_1,
  output VAI1,
  output S15,
  output S14,
  output S13,
  output S12,
  output S11,
  output S10,
  output S9,
  output S8,
  output S7,
  output S6,
  output S5,
  output S4,
  output S3,
  output S2,
  output S1,
  output S0
);

  wire somador_completo_2_bits_2_vai_1, somador_completo_2_bits_3_vai_1, somador_completo_2_bits_4_vai_1,
       somador_completo_2_bits_5_vai_1, somador_completo_2_bits_6_vai_1, somador_completo_2_bits_7_vai_1,
       somador_completo_2_bits_8_vai_1, somador_completo_2_bits_9_vai_1, somador_completo_2_bits_10_vai_1,
       somador_completo_2_bits_11_vai_1, somador_completo_2_bits_12_vai_1, somador_completo_2_bits_13_vai_1,
       somador_completo_2_bits_14_vai_1, somador_completo_2_bits_15_vai_1, somador_completo_2_bits_16_vai_1;

  somador_completo_2_bits somador_completo_2_bits_1 (
    .VEM_1(somador_completo_2_bits_2_vai_1), .A(A15), .B(B15), .SOMA(S15), .VAI_1(VAI1));
  somador_completo_2_bits somador_completo_2_bits_2 (
    .VEM_1(somador_completo_2_bits_3_vai_1), .A(A14), .B(B14), .SOMA(S14),
    .VAI_1(somador_completo_2_bits_2_vai_1));
  somador_completo_2_bits somador_completo_2_bits_3 (
    .VEM_1(somador_completo_2_bits_4_vai_1), .A(A13), .B(B13), .SOMA(S13),
    .VAI_1(somador_completo_2_bits_3_vai_1));
  somador_completo_2_bits somador_completo_2_bits_4 (
    .VEM_1(somador_completo_2_bits_5_vai_1), .A(A12), .B(B12), .SOMA(S12),
    .VAI_1(somador_completo_2_bits_4_vai_1));
  somador_completo_2_bits somador_completo_2_bits_5 (
    .VEM_1(somador_completo_2_bits_6_vai_1), .A(A11), .B(B11), .SOMA(S11),
    .VAI_1(somador_completo_2_bits_5_vai_1));
  somador_completo_2_bits somador_completo_2_bits_6 (
    .VEM_1(somador_completo_2_bits_7_vai_1), .A(A10), .B(B10), .SOMA(S10),
    .VAI_1(somador_completo_2_bits_6_vai_1));
  somador_completo_2_bits somador_completo_2_bits_7 (
    .VEM_1(somador_completo_2_bits_8_vai_1), .A(A9), .B(B9), .SOMA(S9),
    .VAI_1(somador_completo_2_bits_7_vai_1));
  somador_completo_2_bits somador_completo_2_bits_8 (
    .VEM_1(somador_completo_2_bits_9_vai_1), .A(A8), .B(B8), .SOMA(S8),
    .VAI_1(somador_completo_2_bits_8_vai_1));
  somador_completo_2_bits somador_completo_2_bits_9 (
    .VEM_1(somador_completo_2_bits_10_vai_1), .A(A7), .B(B7), .SOMA(S7),
    .VAI_1(somador_completo_2_bits_9_vai_1));
  somador_completo_2_bits somador_completo_2_bits_10 (
    .VEM_1(somador_completo_2_bits_11_vai_1), .A(A6), .B(B6), .SOMA(S6),
    .VAI_1(somador_completo_2_bits_10_vai_1));
  somador_completo_2_bits somador_completo_2_bits_11 (
    .VEM_1(somador_completo_2_bits_12_vai_1), .A(A5), .B(B5), .SOMA(S5),
    .VAI_1(somador_completo_2_bits_11_vai_1));
  somador_completo_2_bits somador_completo_2_bits_12 (
    .VEM_1(somador_completo_2_bits_13_vai_1), .A(A4), .B(B4), .SOMA(S4),
    .VAI_1(somador_completo_2_bits_12_vai_1));
  somador_completo_2_bits somador_completo_2_bits_13 (
    .VEM_1(somador_completo_2_bits_14_vai_1), .A(A3), .B(B3), .SOMA(S3),
    .VAI_1(somador_completo_2_bits_13_vai_1));
  somador_completo_2_bits somador_completo_2_bits_14 (
    .VEM_1(somador_completo_2_bits_15_vai_1), .A(A2), .B(B2), .SOMA(S2),
    .VAI_1(somador_completo_2_bits_14_vai_1));
  somador_completo_2_bits somador_completo_2_bits_15 (
    .VEM_1(somador_completo_2_bits_16_vai_1), .A(A1), .B(B1), .SOMA(S1),
    .VAI_1(somador_completo_2_bits_15_vai_1));
  somador_completo_2_bits somador_completo_2_bits_16 (
    .VEM_1(VEM_1), .A(A0), .B(B0), .SOMA(S0), .VAI_1(somador_completo_2_bits_16_vai_1));
endmodule
