// Logisim project SOMADOR_COMPLETO_1BIT.circ as structural Verilog
module main (
  input  VEM_1,
  input  A,
  input  B,
  output SOMA,
  output VAI_1
);

  wire and_1_out, and_2_out, and_3_out;

  ExactlyOne xor_1 (.out(SOMA), .in0(B), .in1(A), .in2(VEM_1));
  and and_1 (and_1_out, VEM_1, B);
  and and_2 (and_2_out, VEM_1, A);
  and and_3 (and_3_out, A, B);
  or or_1 (VAI_1, and_1_out, and_2_out, and_3_out);

  // Notes on the sheet:
  //   SOMA = VEM1 XOR A XOR B
  //   VAI 1 = (VEM1 AND B) OR (VEM1 AND A) OR (A AND B) 
endmodule
