// Logisim project ULA_1_BIT_4_OPERAÇÕES.circ as structural Verilog
module ULA (
  input  A,
  input  B,
  input  in_3,
  input  in_4,
  output VAI_1,
  output out_6,
  output VAI_1_2,
  output VAI_1_3
);

  wire \multiplicador_1_multiplicação , nand_1_out, somador_1_soma, \subtrator_1_subtração ;

  SOMADOR somador_1 (.VEM_1(1'b0), .A(A), .B(B), .SOMA(somador_1_soma), .VAI_1(VAI_1));
  SUBTRATOR subtrator_1 (.VEM_1(1'b0), .A(A), .B(B), .\SUBTRAÇÃO (\subtrator_1_subtração ), .VAI_1(VAI_1_2));
  MULTIPLICADOR multiplicador_1 (
    .VEM_1(1'b0), .A(A), .B(B), .\MULTIPLICAÇÃO (\multiplicador_1_multiplicação ), .VAI_1(VAI_1_3));
  nand nand_1 (nand_1_out, A, B);
  MUX_4 mux_4_1 (
    .Entrada_0(somador_1_soma), .Entrada_1(\subtrator_1_subtração ),
    .Entrada_2(\multiplicador_1_multiplicação ), .Entrada_3(nand_1_out), .Seletor_B(in_3), .Seletor_A(in_4),
    .out_7(out_6));

  // Notes on the sheet:
  //   0 0 = SOMA
  //   0 1 = SUBTRAI
  //   1 0 = MULTIPLICA
  //   1 1 = NAND
endmodule
