// Logisim project projeto-entrega1.circ as structural Verilog
module main (
  input  [31:0] in_1,
  input  [31:0] in_2,
  input  [4:0] in_3,
  output [31:0] out_4
);

  wire ula_32_1_overflow_soma;

  Hex_Digit_Display hex_digit_display_1 (.value(in_1[27:24]));  // open: dp
  Hex_Digit_Display hex_digit_display_2 (.value(in_1[31:28]));  // open: dp
  Hex_Digit_Display hex_digit_display_3 (.value(in_2[31:28]));  // open: dp
  Hex_Digit_Display hex_digit_display_4 (.value(in_2[27:24]));  // open: dp
  Hex_Digit_Display hex_digit_display_5 (.value(in_1[19:16]));  // open: dp
  Hex_Digit_Display hex_digit_display_6 (.value(in_1[23:20]));  // open: dp
  Hex_Digit_Display hex_digit_display_7 (.value(in_2[23:20]));  // open: dp
  Hex_Digit_Display hex_digit_display_8 (.value(in_2[19:16]));  // open: dp
  Hex_Digit_Display hex_digit_display_9 (.value(in_1[11:8]));  // open: dp
  Hex_Digit_Display hex_digit_display_10 (.value(in_1[15:12]));  // open: dp
  Hex_Digit_Display hex_digit_display_11 (.value(in_2[11:8]));  // open: dp
  Hex_Digit_Display hex_digit_display_12 (.value(in_2[15:12]));  // open: dp
  Hex_Digit_Display hex_digit_display_13 (.value(in_1[3:0]));  // open: dp
  Hex_Digit_Display hex_digit_display_14 (.value(in_1[7:4]));  // open: dp
  Hex_Digit_Display hex_digit_display_15 (.value(in_2[7:4]));  // open: dp
  Hex_Digit_Display hex_digit_display_16 (.value(in_2[3:0]));  // open: dp
  LED OVERFLOW_SOMA (.in(ula_32_1_overflow_soma));
  Hex_Digit_Display hex_digit_display_17 (.value(out_4[31:28]));  // open: dp
  ULA_32 ula_32_1 (.A(in_1), .B(in_2), .U(out_4), .\Operação (in_3), .OVERFLOW_SOMA(ula_32_1_overflow_soma));
  Hex_Digit_Display hex_digit_display_18 (.value(out_4[27:24]));  // open: dp
  Hex_Digit_Display hex_digit_display_19 (.value(out_4[23:20]));  // open: dp
  Hex_Digit_Display hex_digit_display_20 (.value(out_4[15:12]));  // open: dp
  Hex_Digit_Display hex_digit_display_21 (.value(out_4[19:16]));  // open: dp
  Hex_Digit_Display hex_digit_display_22 (.value(out_4[7:4]));  // open: dp
  Hex_Digit_Display hex_digit_display_23 (.value(out_4[11:8]));  // open: dp
  Hex_Digit_Display hex_digit_display_24 (.value(out_4[3:0]));  // open: dp
endmodule

module mux16 (
  input  Canal_0,
  input  Canal_1,
  input  Canal_2,
  input  Canal_3,
  input  Canal_4,
  input  Canal_5,
  input  Canal_6,
  input  Canal_7,
  input  Canal_8,
  input  Canal_9,
  input  Canal_10,
  input  Canal_11,
  input  Canal_12,
  input  Canal_13,
  input  Canal_14,
  input  Canal_15,
  input  SEL_3,
  input  SEL_2,
  input  SEL_1,
  input  SEL_0,
  output out_21
);

  wire mux8_1_saida, mux8_2_saida;

  mux8 mux8_1 (
    .Canal_0(Canal_0), .Canal_1(Canal_1), .Canal_2(Canal_2), .Canal_3(Canal_3), .Canal_4(Canal_4),
    .Canal_5(Canal_5), .Canal_6(Canal_6), .Canal_7(Canal_7), .Saida(mux8_1_saida), .Sel_2(SEL_2),
    .Sel_1(SEL_1), .Sel_0(SEL_0));
  mux8 mux8_2 (
    .Canal_0(Canal_8), .Canal_1(Canal_9), .Canal_2(Canal_10), .Canal_3(Canal_11), .Canal_4(Canal_12),
    .Canal_5(Canal_13), .Canal_6(Canal_14), .Canal_7(Canal_15), .Saida(mux8_2_saida), .Sel_2(SEL_2),
    .Sel_1(SEL_1), .Sel_0(SEL_0));
  mux2 mux2_1 (.Canal_0(mux8_1_saida), .Canal_1(mux8_2_saida), .out_4(out_21), .Seletor_0(SEL_3));
endmodule

module mux8 (
  input  Canal_0,
  input  Canal_1,
  input  Canal_2,
  input  Canal_3,
  input  Canal_4,
  input  Canal_5,
  input  Canal_6,
  input  Canal_7,
  input  Sel_2,
  input  Sel_1,
  input  Sel_0,
  output Saida
);

  wire and_1_out, and_2_out, and_3_out, and_4_out, and_5_out, and_6_out, and_7_out, and_8_out;

  and and_1 (and_1_out, Canal_0, ~Sel_2, ~Sel_1, ~Sel_0);  // AND_Gate
  and and_2 (and_2_out, Canal_1, ~Sel_2, ~Sel_1, Sel_0);  // AND_Gate
  and and_3 (and_3_out, Canal_2, ~Sel_2, Sel_1, ~Sel_0);  // AND_Gate
  and and_4 (and_4_out, Canal_3, ~Sel_2, Sel_1, Sel_0);  // AND_Gate
  and and_5 (and_5_out, Canal_4, Sel_2, ~Sel_1, ~Sel_0);  // AND_Gate
  and and_6 (and_6_out, Canal_5, Sel_2, ~Sel_1, Sel_0);  // AND_Gate
  and and_7 (and_7_out, Canal_6, Sel_2, Sel_1, ~Sel_0);  // AND_Gate
  and and_8 (and_8_out, Canal_7, Sel_2, Sel_1, Sel_0);
  or or_1 (Saida, and_1_out, and_2_out, and_3_out, and_4_out, and_5_out, and_6_out, and_7_out, and_8_out);
endmodule

module mux2 (
  input  Canal_0,
  input  Canal_1,
  input  Seletor_0,
  output out_4
);

  wire and_1_out, and_2_out;

  and and_1 (and_1_out, Canal_0, ~Seletor_0);  // AND_Gate
  and and_2 (and_2_out, Canal_1, Seletor_0);
  or or_1 (out_4, and_1_out, and_2_out);
endmodule

module ULA_1_BIT (
  input  A,
  input  B,
  input  VEM_1,
  input  VEM_1_2,
  input  [4:0] in_5,
  output U,
  output VAI_1,
  output VAI_1_2
);

  wire and_1_out, or_1_out, soma_1_soma, \subtração_1_subtração , xor_1_out;

  and and_1 (and_1_out, A, B);
  or or_1 (or_1_out, A, B);
  xor xor_1 (xor_1_out, A, B);
  SOMA soma_1 (.SOMA(soma_1_soma), .VAI_1(VAI_1), .VEM_1(VEM_1), .B(B), .A(A));
  \SUBTRAÇÃO  \subtração_1  (.\SUBTRAÇÃO (\subtração_1_subtração ), .VAI_1(VAI_1_2), .VEM_1(VEM_1_2), .B(B), .A(A));
  mux32 mux32_1 (
    .out_38(U), .I(\subtração_1_subtração ), .H(B), .G(B), .F(B), .E(B), .D(soma_1_soma), .C(xor_1_out),
    .B(or_1_out), .A(and_1_out), .SEL_0(in_5[0]), .SEL_1(in_5[1]), .SEL_2(in_5[2]), .SEL_3(in_5[3]),
    .SEL_4(in_5[4]));  // open: P, Z6, O, Z5, N, Z4, M, Z3, L, Z2, K, Z1, J, Z, Y, X, W, V, U, T, S, R, Q
endmodule

module SOMA (
  input  VEM_1,
  input  B,
  input  A,
  output SOMA,
  output VAI_1
);

  wire and_1_out, and_2_out, and_3_out, xor_1_out;

  xor xor_1 (xor_1_out, B, A);
  and and_1 (and_1_out, A, VEM_1);
  and and_2 (and_2_out, B, VEM_1);
  and and_3 (and_3_out, A, B);
  xor xor_2 (SOMA, xor_1_out, VEM_1);
  or or_1 (VAI_1, and_1_out, and_2_out, and_3_out);
endmodule

module ULA_4BIT (
  input  [3:0] A,
  input  [3:0] B,
  input  [4:0] in_3,
  output [3:0] U,
  output OVERFLOW
);

  wire _0VAI1, _1VAI1, _2VAI1;

  ULA_1_BIT ula_1_bit_1 (
    .VAI_1(_0VAI1), .U(U[0]), .VEM_1(1'b0), .A(A[0]), .B(B[0]), .in_5(in_3));  // open: VEM_1_2, VAI_1_2
  ULA_1_BIT ula_1_bit_2 (
    .VAI_1(_1VAI1), .U(U[1]), .VEM_1(_0VAI1), .A(A[1]), .B(B[1]), .in_5(in_3));  // open: VEM_1_2, VAI_1_2
  ULA_1_BIT ula_1_bit_3 (
    .VAI_1(_2VAI1), .U(U[2]), .VEM_1(_1VAI1), .A(A[2]), .B(B[2]), .in_5(in_3));  // open: VEM_1_2, VAI_1_2
  ULA_1_BIT ula_1_bit_4 (
    .VAI_1(OVERFLOW), .U(U[3]), .VEM_1(_2VAI1), .A(A[3]), .B(B[3]), .in_5(in_3));  // open: VEM_1_2, VAI_1_2

  // Other names for the same wires on the sheet: SELETOR[4:0] = in_3

  // Notes on the sheet:
  //   000 = AND
  //   001 = OR
  //   010 = XOR
  //   011 = SOMA
endmodule

module ULA_32 (
  input  [31:0] B,
  input  [31:0] A,
  input  [4:0] \Operação ,
  output OVERFLOW_SOMA,
  output [31:0] U
);

  wire _0VAI1, _1VAI1, _2VAI1, _3VAI1, _4VAI1, _5VAI1, _6VAI1, _7VAI1, _8VAI1, _9VAI1, _10VAI1, _11VAI1,
       _12VAI1, _13VAI1, _14VAI1, _15VAI1, _16VAI1, _17VAI1, _18VAI1, _19VAI1, _20VAI1, _21VAI1, _22VAI1,
       _23VAI1, _24VAI1, _25VAI1, _26VAI1, _27VAI1, _28VAI1, _29VAI1, _30VAI1, B0, B1, B2, B3, B4, B5, B6,
       B7, B8, B9, B10, B11, B12, B13, B14, B15, B16, B17, B18, B19, B20, B21, B22, B23, B24, B25, B26, B27,
       B28, B29, B30, B31, sla_detect_1_out_2, sll_detect_1_out_2, sra_detect_1_out_2, srl_detect_1_out_2,
       ula_1_bit_4_vai_1_2, ula_1_bit_5_vai_1_2, ula_1_bit_6_vai_1_2, ula_1_bit_7_vai_1_2,
       ula_1_bit_8_vai_1_2, ula_1_bit_9_vai_1_2, ula_1_bit_10_vai_1_2, ula_1_bit_11_vai_1_2,
       ula_1_bit_12_vai_1_2, ula_1_bit_13_vai_1_2, ula_1_bit_14_vai_1_2, ula_1_bit_15_vai_1_2,
       ula_1_bit_16_vai_1_2, ula_1_bit_17_vai_1_2, ula_1_bit_18_vai_1_2, ula_1_bit_19_vai_1_2,
       ula_1_bit_20_vai_1_2, ula_1_bit_21_vai_1_2, ula_1_bit_22_vai_1_2, ula_1_bit_23_vai_1_2,
       ula_1_bit_24_vai_1_2, ula_1_bit_25_vai_1_2, ula_1_bit_26_vai_1_2, ula_1_bit_27_vai_1_2,
       ula_1_bit_28_vai_1_2, ula_1_bit_29_vai_1_2, ula_1_bit_30_vai_1_2, ula_1_bit_31_vai_1_2,
       ula_1_bit_32_vai_1_2, VAI_19, VAI_29, VAI_A9;
  wire [31:0] sll_1_out_3, sra_1_out_3, srl_1_out_3;

  ULA_1_BIT ula_1_bit_1 (
    .VAI_1(_9VAI1), .U(U[9]), .VEM_1(_8VAI1), .A(A[9]), .B(B9), .in_5(\Operação ),
    .VEM_1_2(ula_1_bit_4_vai_1_2), .VAI_1_2(VAI_A9));
  ULA_1_BIT ula_1_bit_2 (
    .VAI_1(_19VAI1), .U(U[19]), .VEM_1(_18VAI1), .A(A[19]), .B(B19), .in_5(\Operação ),
    .VEM_1_2(ula_1_bit_5_vai_1_2), .VAI_1_2(VAI_19));
  ULA_1_BIT ula_1_bit_3 (
    .VAI_1(_29VAI1), .U(U[29]), .VEM_1(_28VAI1), .A(A[29]), .B(B19), .in_5(\Operação ),
    .VEM_1_2(ula_1_bit_6_vai_1_2), .VAI_1_2(VAI_29));
  ULA_1_BIT ula_1_bit_4 (
    .VAI_1(_8VAI1), .U(U[8]), .VEM_1(_7VAI1), .A(A[8]), .B(B8), .in_5(\Operação ),
    .VEM_1_2(ula_1_bit_7_vai_1_2), .VAI_1_2(ula_1_bit_4_vai_1_2));
  ULA_1_BIT ula_1_bit_5 (
    .VAI_1(_18VAI1), .U(U[18]), .VEM_1(_17VAI1), .A(A[18]), .B(B18), .in_5(\Operação ),
    .VEM_1_2(ula_1_bit_8_vai_1_2), .VAI_1_2(ula_1_bit_5_vai_1_2));
  ULA_1_BIT ula_1_bit_6 (
    .VAI_1(_28VAI1), .U(U[28]), .VEM_1(_27VAI1), .A(A[28]), .B(B28), .in_5(\Operação ),
    .VEM_1_2(ula_1_bit_9_vai_1_2), .VAI_1_2(ula_1_bit_6_vai_1_2));
  ULA_1_BIT ula_1_bit_7 (
    .VAI_1(_7VAI1), .U(U[7]), .VEM_1(_6VAI1), .A(A[7]), .B(B7), .in_5(\Operação ),
    .VEM_1_2(ula_1_bit_10_vai_1_2), .VAI_1_2(ula_1_bit_7_vai_1_2));
  ULA_1_BIT ula_1_bit_8 (
    .VAI_1(_17VAI1), .U(U[17]), .VEM_1(_16VAI1), .A(A[17]), .B(B17), .in_5(\Operação ),
    .VEM_1_2(ula_1_bit_11_vai_1_2), .VAI_1_2(ula_1_bit_8_vai_1_2));
  ULA_1_BIT ula_1_bit_9 (
    .VAI_1(_27VAI1), .U(U[27]), .VEM_1(_26VAI1), .A(A[27]), .B(B27), .in_5(\Operação ),
    .VEM_1_2(ula_1_bit_12_vai_1_2), .VAI_1_2(ula_1_bit_9_vai_1_2));
  ULA_1_BIT ula_1_bit_10 (
    .VAI_1(_6VAI1), .U(U[6]), .VEM_1(_5VAI1), .A(A[6]), .B(B6), .in_5(\Operação ),
    .VEM_1_2(ula_1_bit_13_vai_1_2), .VAI_1_2(ula_1_bit_10_vai_1_2));
  ULA_1_BIT ula_1_bit_11 (
    .VAI_1(_16VAI1), .U(U[16]), .VEM_1(_15VAI1), .A(A[16]), .B(B16), .in_5(\Operação ),
    .VEM_1_2(ula_1_bit_14_vai_1_2), .VAI_1_2(ula_1_bit_11_vai_1_2));
  ULA_1_BIT ula_1_bit_12 (
    .VAI_1(_26VAI1), .U(U[26]), .VEM_1(_25VAI1), .A(A[26]), .B(B26), .in_5(\Operação ),
    .VEM_1_2(ula_1_bit_15_vai_1_2), .VAI_1_2(ula_1_bit_12_vai_1_2));
  SRL srl_1 (.in_1(sll_1_out_3), .in_2(srl_detect_1_out_2), .out_3(srl_1_out_3));
  SLL sll_1 (.in_1(B), .in_2(sll_detect_1_out_2), .out_3(sll_1_out_3));
  SRL_Detect srl_detect_1 (.out_2(srl_detect_1_out_2), .in_1(\Operação ));
  SLL_Detect sll_detect_1 (.out_2(sll_detect_1_out_2), .in_1(\Operação ));
  SRA sra_1 (.in_1(srl_1_out_3), .in_2(sra_detect_1_out_2), .out_3(sra_1_out_3));
  SLA_DETECT sla_detect_1 (.out_2(sla_detect_1_out_2), .in_1(\Operação ));
  SRA_Detect sra_detect_1 (.out_2(sra_detect_1_out_2), .in_1(\Operação ));
  ULA_1_BIT ula_1_bit_13 (
    .VAI_1(_5VAI1), .U(U[5]), .VEM_1(_4VAI1), .A(A[5]), .B(B5), .in_5(\Operação ),
    .VEM_1_2(ula_1_bit_16_vai_1_2), .VAI_1_2(ula_1_bit_13_vai_1_2));
  ULA_1_BIT ula_1_bit_14 (
    .VAI_1(_15VAI1), .U(U[15]), .VEM_1(_14VAI1), .A(A[15]), .B(B15), .in_5(\Operação ),
    .VEM_1_2(ula_1_bit_17_vai_1_2), .VAI_1_2(ula_1_bit_14_vai_1_2));
  ULA_1_BIT ula_1_bit_15 (
    .VAI_1(_25VAI1), .U(U[25]), .VEM_1(_24VAI1), .A(A[25]), .B(B25), .in_5(\Operação ),
    .VEM_1_2(ula_1_bit_18_vai_1_2), .VAI_1_2(ula_1_bit_15_vai_1_2));
  SLA sla_1 (
    .in_1(sra_1_out_3), .in_2(sla_detect_1_out_2),
    .out_3({B31, B30, B29, B28, B27, B26, B25, B24, B23, B22, B21, B20, B19, B18, B17, B16, B15, B14, B13, B12, B11, B10, B9, B8, B7, B6, B5, B4, B3, B2, B1, B0}));
  ULA_1_BIT ula_1_bit_16 (
    .VAI_1(_4VAI1), .U(U[4]), .VEM_1(_3VAI1), .A(A[4]), .B(B4), .in_5(\Operação ),
    .VEM_1_2(ula_1_bit_19_vai_1_2), .VAI_1_2(ula_1_bit_16_vai_1_2));
  ULA_1_BIT ula_1_bit_17 (
    .VAI_1(_14VAI1), .U(U[14]), .VEM_1(_13VAI1), .A(A[14]), .B(B14), .in_5(\Operação ),
    .VEM_1_2(ula_1_bit_20_vai_1_2), .VAI_1_2(ula_1_bit_17_vai_1_2));
  ULA_1_BIT ula_1_bit_18 (
    .VAI_1(_24VAI1), .U(U[24]), .VEM_1(_23VAI1), .A(A[24]), .B(B24), .in_5(\Operação ),
    .VEM_1_2(ula_1_bit_21_vai_1_2), .VAI_1_2(ula_1_bit_18_vai_1_2));
  ULA_1_BIT ula_1_bit_19 (
    .VAI_1(_3VAI1), .U(U[3]), .VEM_1(_2VAI1), .A(A[3]), .B(B3), .in_5(\Operação ),
    .VEM_1_2(ula_1_bit_22_vai_1_2), .VAI_1_2(ula_1_bit_19_vai_1_2));
  ULA_1_BIT ula_1_bit_20 (
    .VAI_1(_13VAI1), .U(U[13]), .VEM_1(_12VAI1), .A(A[13]), .B(B13), .in_5(\Operação ),
    .VEM_1_2(ula_1_bit_23_vai_1_2), .VAI_1_2(ula_1_bit_20_vai_1_2));
  ULA_1_BIT ula_1_bit_21 (
    .VAI_1(_23VAI1), .U(U[23]), .VEM_1(_22VAI1), .A(A[23]), .B(B23), .in_5(\Operação ),
    .VEM_1_2(ula_1_bit_24_vai_1_2), .VAI_1_2(ula_1_bit_21_vai_1_2));
  ULA_1_BIT ula_1_bit_22 (
    .VAI_1(_2VAI1), .U(U[2]), .VEM_1(_1VAI1), .A(A[2]), .B(B2), .in_5(\Operação ),
    .VEM_1_2(ula_1_bit_25_vai_1_2), .VAI_1_2(ula_1_bit_22_vai_1_2));
  ULA_1_BIT ula_1_bit_23 (
    .VAI_1(_12VAI1), .U(U[12]), .VEM_1(_11VAI1), .A(A[12]), .B(B12), .in_5(\Operação ),
    .VEM_1_2(ula_1_bit_26_vai_1_2), .VAI_1_2(ula_1_bit_23_vai_1_2));
  ULA_1_BIT ula_1_bit_24 (
    .VAI_1(_22VAI1), .U(U[22]), .VEM_1(_21VAI1), .A(A[22]), .B(B22), .in_5(\Operação ),
    .VEM_1_2(ula_1_bit_27_vai_1_2), .VAI_1_2(ula_1_bit_24_vai_1_2));
  LED \OVERFLOW__SUBTRAÇÃO  (.in(ula_1_bit_28_vai_1_2));
  ULA_1_BIT ula_1_bit_25 (
    .VAI_1(_1VAI1), .U(U[1]), .VEM_1(_0VAI1), .A(A[1]), .B(B1), .in_5(\Operação ),
    .VEM_1_2(ula_1_bit_30_vai_1_2), .VAI_1_2(ula_1_bit_25_vai_1_2));
  ULA_1_BIT ula_1_bit_26 (
    .VAI_1(_11VAI1), .U(U[11]), .VEM_1(_10VAI1), .A(A[11]), .B(B11), .in_5(\Operação ),
    .VEM_1_2(ula_1_bit_31_vai_1_2), .VAI_1_2(ula_1_bit_26_vai_1_2));
  ULA_1_BIT ula_1_bit_27 (
    .VAI_1(_21VAI1), .U(U[21]), .VEM_1(_20VAI1), .A(A[21]), .B(B21), .in_5(\Operação ),
    .VEM_1_2(ula_1_bit_32_vai_1_2), .VAI_1_2(ula_1_bit_27_vai_1_2));
  ULA_1_BIT ula_1_bit_28 (
    .VAI_1(OVERFLOW_SOMA), .U(U[31]), .VEM_1(_30VAI1), .A(A[31]), .B(B31), .in_5(\Operação ),
    .VEM_1_2(ula_1_bit_29_vai_1_2), .VAI_1_2(ula_1_bit_28_vai_1_2));
  MENU menu_1 ();
  ULA_1_BIT ula_1_bit_29 (
    .VAI_1(_30VAI1), .U(U[30]), .VEM_1(_29VAI1), .A(A[30]), .B(B30), .in_5(\Operação ), .VEM_1_2(VAI_29),
    .VAI_1_2(ula_1_bit_29_vai_1_2));
  ULA_1_BIT ula_1_bit_30 (
    .VAI_1(_0VAI1), .U(U[0]), .VEM_1(1'b0), .A(A[0]), .B(B0), .in_5(\Operação ), .VEM_1_2(1'b0),
    .VAI_1_2(ula_1_bit_30_vai_1_2));
  ULA_1_BIT ula_1_bit_31 (
    .VAI_1(_10VAI1), .U(U[10]), .VEM_1(_9VAI1), .A(A[10]), .B(B10), .in_5(\Operação ), .VEM_1_2(VAI_A9),
    .VAI_1_2(ula_1_bit_31_vai_1_2));
  ULA_1_BIT ula_1_bit_32 (
    .VAI_1(_20VAI1), .U(U[20]), .VEM_1(_19VAI1), .A(A[20]), .B(B20), .in_5(\Operação ), .VEM_1_2(VAI_19),
    .VAI_1_2(ula_1_bit_32_vai_1_2));

  // Other names for the same wires on the sheet: _31VAI1 = OVERFLOW_SOMA
endmodule

module mux32 (
  input  P,
  input  O,
  input  N,
  input  M,
  input  L,
  input  K,
  input  J,
  input  I,
  input  H,
  input  G,
  input  F,
  input  E,
  input  D,
  input  C,
  input  B,
  input  A,
  input  Z6,
  input  Z5,
  input  Z4,
  input  Z3,
  input  Z2,
  input  Z1,
  input  Z,
  input  Y,
  input  X,
  input  W,
  input  V,
  input  U,
  input  T,
  input  S,
  input  R,
  input  Q,
  input  SEL_4,
  input  SEL_3,
  input  SEL_2,
  input  SEL_1,
  input  SEL_0,
  output out_38
);

  wire mux16_1_out_21, mux16_2_out_21;

  mux16 mux16_1 (
    .out_21(mux16_1_out_21), .Canal_0(A), .Canal_1(B), .Canal_2(C), .Canal_3(D), .Canal_4(E), .Canal_5(F),
    .Canal_6(G), .Canal_7(H), .Canal_8(I), .Canal_9(J), .Canal_10(K), .Canal_11(L), .Canal_12(M),
    .Canal_13(N), .Canal_14(O), .Canal_15(P), .SEL_0(SEL_0), .SEL_1(SEL_1), .SEL_2(SEL_2), .SEL_3(SEL_3));
  mux16 mux16_2 (
    .out_21(mux16_2_out_21), .Canal_0(Q), .Canal_1(R), .Canal_2(S), .Canal_3(T), .Canal_4(U), .Canal_5(V),
    .Canal_6(W), .Canal_7(X), .Canal_8(Y), .Canal_9(Z), .Canal_10(Z1), .Canal_11(Z2), .Canal_12(Z3),
    .Canal_13(Z4), .Canal_14(Z5), .Canal_15(Z6), .SEL_0(SEL_0), .SEL_1(SEL_1), .SEL_2(SEL_2), .SEL_3(SEL_3));
  mux2 mux2_1 (.Canal_0(mux16_1_out_21), .Canal_1(mux16_2_out_21), .out_4(out_38), .Seletor_0(SEL_4));
endmodule

module SLL (
  input  [31:0] in_1,
  input  in_2,
  output [31:0] out_3
);

  \MUXÃO___32bits  \muxão_32bits_1  (.Canal_0(in_1), .Canal_1({in_1[30:0], 1'b0}), .\Saída (out_3), .Seletor(in_2));
  Multiplexer #(.width(32), .enable("false")) multiplexer_1 ();  // open: in0, in1, out, sel

  // Notes on the sheet:
  //   Andar um bit para esquerda
endmodule

module SRL (
  input  [31:0] in_1,
  input  in_2,
  output [31:0] out_3
);

  \MUXÃO___32bits  \muxão_32bits_1  (.Canal_0(in_1), .Canal_1({1'b0, in_1[31:1]}), .\Saída (out_3), .Seletor(in_2));
  Multiplexer #(.width(32), .enable("false")) multiplexer_1 ();  // open: in0, in1, out, sel

  // Notes on the sheet:
  //   Andar um bit para direita
endmodule

module SRA (
  input  [31:0] in_1,
  input  in_2,
  output [31:0] out_3
);

  \MUXÃO___32bits  \muxão_32bits_1  (
    .Canal_0(in_1), .Canal_1({{2{in_1[31]}}, in_1[30:1]}), .\Saída (out_3), .Seletor(in_2));
  Multiplexer #(.width(32), .enable("false")) multiplexer_1 ();  // open: in0, in1, out, sel

  // Notes on the sheet:
  //   Andar um bit para direita mantendo o sinal
endmodule

// SLLD
module SLL_Detect (
  input  [4:0] in_1,
  output out_2
);

  and and_1 (out_2, ~in_1[4], ~in_1[3], in_1[2], ~in_1[1], ~in_1[0]);  // AND_Gate
endmodule

// SRLD
module SRL_Detect (
  input  [4:0] in_1,
  output out_2
);

  and and_1 (out_2, ~in_1[4], ~in_1[3], in_1[2], ~in_1[1], in_1[0]);  // AND_Gate
endmodule

// SRAD
module SRA_Detect (
  input  [4:0] in_1,
  output out_2
);

  and and_1 (out_2, ~in_1[4], ~in_1[3], in_1[2], in_1[1], ~in_1[0]);  // AND_Gate
endmodule

module \MUXÃO___32bits  (
  input  Seletor,
  input  [31:0] Canal_0,
  input  [31:0] Canal_1,
  output [31:0] \Saída 
);

  mux2 mux2_1 (.Canal_0(Canal_0[15]), .Canal_1(Canal_1[15]), .out_4(\Saída [15]), .Seletor_0(Seletor));
  mux2 mux2_2 (.Canal_0(Canal_0[16]), .Canal_1(Canal_1[16]), .out_4(\Saída [16]), .Seletor_0(Seletor));
  mux2 mux2_3 (.Canal_0(Canal_0[14]), .Canal_1(Canal_1[14]), .out_4(\Saída [14]), .Seletor_0(Seletor));
  mux2 mux2_4 (.Canal_0(Canal_0[17]), .Canal_1(Canal_1[17]), .out_4(\Saída [17]), .Seletor_0(Seletor));
  mux2 mux2_5 (.Canal_0(Canal_0[13]), .Canal_1(Canal_1[13]), .out_4(\Saída [13]), .Seletor_0(Seletor));
  mux2 mux2_6 (.Canal_0(Canal_0[18]), .Canal_1(Canal_1[18]), .out_4(\Saída [18]), .Seletor_0(Seletor));
  mux2 mux2_7 (.Canal_0(Canal_0[12]), .Canal_1(Canal_1[12]), .out_4(\Saída [12]), .Seletor_0(Seletor));
  mux2 mux2_8 (.Canal_0(Canal_0[19]), .Canal_1(Canal_1[19]), .out_4(\Saída [19]), .Seletor_0(Seletor));
  mux2 mux2_9 (.Canal_0(Canal_0[11]), .Canal_1(Canal_1[11]), .out_4(\Saída [11]), .Seletor_0(Seletor));
  mux2 mux2_10 (.Canal_0(Canal_0[20]), .Canal_1(Canal_1[20]), .out_4(\Saída [20]), .Seletor_0(Seletor));
  mux2 mux2_11 (.Canal_0(Canal_0[10]), .Canal_1(Canal_1[10]), .out_4(\Saída [10]), .Seletor_0(Seletor));
  mux2 mux2_12 (.Canal_0(Canal_0[21]), .Canal_1(Canal_1[21]), .out_4(\Saída [21]), .Seletor_0(Seletor));
  mux2 mux2_13 (.Canal_0(Canal_0[9]), .Canal_1(Canal_1[9]), .out_4(\Saída [9]), .Seletor_0(Seletor));
  mux2 mux2_14 (.Canal_0(Canal_0[22]), .Canal_1(Canal_1[22]), .out_4(\Saída [22]), .Seletor_0(Seletor));
  mux2 mux2_15 (.Canal_0(Canal_0[8]), .Canal_1(Canal_1[8]), .out_4(\Saída [8]), .Seletor_0(Seletor));
  mux2 mux2_16 (.Canal_0(Canal_0[23]), .Canal_1(Canal_1[23]), .out_4(\Saída [23]), .Seletor_0(Seletor));
  mux2 mux2_17 (.Canal_0(Canal_0[7]), .Canal_1(Canal_1[7]), .out_4(\Saída [7]), .Seletor_0(Seletor));
  mux2 mux2_18 (.Canal_0(Canal_0[24]), .Canal_1(Canal_1[24]), .out_4(\Saída [24]), .Seletor_0(Seletor));
  mux2 mux2_19 (.Canal_0(Canal_0[6]), .Canal_1(Canal_1[6]), .out_4(\Saída [6]), .Seletor_0(Seletor));
  mux2 mux2_20 (.Canal_0(Canal_0[25]), .Canal_1(Canal_1[25]), .out_4(\Saída [25]), .Seletor_0(Seletor));
  mux2 mux2_21 (.Canal_0(Canal_0[5]), .Canal_1(Canal_1[5]), .out_4(\Saída [5]), .Seletor_0(Seletor));
  mux2 mux2_22 (.Canal_0(Canal_0[26]), .Canal_1(Canal_1[26]), .out_4(\Saída [26]), .Seletor_0(Seletor));
  mux2 mux2_23 (.Canal_0(Canal_0[4]), .Canal_1(Canal_1[4]), .out_4(\Saída [4]), .Seletor_0(Seletor));
  mux2 mux2_24 (.Canal_0(Canal_0[27]), .Canal_1(Canal_1[27]), .out_4(\Saída [27]), .Seletor_0(Seletor));
  mux2 mux2_25 (.Canal_0(Canal_0[3]), .Canal_1(Canal_1[3]), .out_4(\Saída [3]), .Seletor_0(Seletor));
  mux2 mux2_26 (.Canal_0(Canal_0[28]), .Canal_1(Canal_1[28]), .out_4(\Saída [28]), .Seletor_0(Seletor));
  mux2 mux2_27 (.Canal_0(Canal_0[2]), .Canal_1(Canal_1[2]), .out_4(\Saída [2]), .Seletor_0(Seletor));
  mux2 mux2_28 (.Canal_0(Canal_0[29]), .Canal_1(Canal_1[29]), .out_4(\Saída [29]), .Seletor_0(Seletor));
  mux2 mux2_29 (.Canal_0(Canal_0[1]), .Canal_1(Canal_1[1]), .out_4(\Saída [1]), .Seletor_0(Seletor));
  mux2 mux2_30 (.Canal_0(Canal_0[30]), .Canal_1(Canal_1[30]), .out_4(\Saída [30]), .Seletor_0(Seletor));
  mux2 mux2_31 (.Canal_0(Canal_0[0]), .Canal_1(Canal_1[0]), .out_4(\Saída [0]), .Seletor_0(Seletor));
  mux2 mux2_32 (.Canal_0(Canal_0[31]), .Canal_1(Canal_1[31]), .out_4(\Saída [31]), .Seletor_0(Seletor));

  // Other names for the same wires on the sheet: A0 = Canal_0[0]; A1 = Canal_0[1]; A2 = Canal_0[2]; A3 = Canal_0[3];
  //   A4 = Canal_0[4]; A5 = Canal_0[5]; A6 = Canal_0[6]; A7 = Canal_0[7]; A8 = Canal_0[8]; A9 = Canal_0[9];
  //   A10 = Canal_0[10]; A11 = Canal_0[11]; A12 = Canal_0[12]; A13 = Canal_0[13]; A14 = Canal_0[14];
  //   A15 = Canal_0[15]; A16 = Canal_0[16]; A17 = Canal_0[17]; A18 = Canal_0[18]; A19 = Canal_0[19];
  //   A20 = Canal_0[20]; A21 = Canal_0[21]; A22 = Canal_0[22]; A23 = Canal_0[23]; A24 = Canal_0[24];
  //   A25 = Canal_0[25]; A26 = Canal_0[26]; A27 = Canal_0[27]; A28 = Canal_0[28]; A29 = Canal_0[29];
  //   A30 = Canal_0[30]; A31 = Canal_0[31]; B0 = Canal_1[0]; B1 = Canal_1[1]; B2 = Canal_1[2]; B3 = Canal_1[3];
  //   B4 = Canal_1[4]; B5 = Canal_1[5]; B6 = Canal_1[6]; B7 = Canal_1[7]; B8 = Canal_1[8]; B9 = Canal_1[9];
  //   B10 = Canal_1[10]; B11 = Canal_1[11]; B12 = Canal_1[12]; B13 = Canal_1[13]; B14 = Canal_1[14];
  //   B15 = Canal_1[15]; B16 = Canal_1[16]; B17 = Canal_1[17]; B18 = Canal_1[18]; B19 = Canal_1[19];
  //   B20 = Canal_1[20]; B21 = Canal_1[21]; B22 = Canal_1[22]; B23 = Canal_1[23]; B24 = Canal_1[24];
  //   B25 = Canal_1[25]; B26 = Canal_1[26]; B27 = Canal_1[27]; B28 = Canal_1[28]; B29 = Canal_1[29];
  //   B30 = Canal_1[30]; B31 = Canal_1[31]; S0 = \Saída [0]; S1 = \Saída [1]; S2 = \Saída [2]; S3 = \Saída [3];
  //   S4 = \Saída [4]; S5 = \Saída [5]; S6 = \Saída [6]; S7 = \Saída [7]; S8 = \Saída [8]; S9 = \Saída [9];
  //   S10 = \Saída [10]; S11 = \Saída [11]; S12 = \Saída [12]; S13 = \Saída [13]; S14 = \Saída [14];
  //   S15 = \Saída [15]; S16 = \Saída [16]; S17 = \Saída [17]; S18 = \Saída [18]; S19 = \Saída [19];
  //   S20 = \Saída [20]; S21 = \Saída [21]; S22 = \Saída [22]; S23 = \Saída [23]; S24 = \Saída [24];
  //   S25 = \Saída [25]; S26 = \Saída [26]; S27 = \Saída [27]; S28 = \Saída [28]; S29 = \Saída [29];
  //   S30 = \Saída [30]; S31 = \Saída [31]
endmodule

// SLAD
module SLA_DETECT (
  input  [4:0] in_1,
  output out_2
);

  and and_1 (out_2, ~in_1[4], ~in_1[3], in_1[2], in_1[1], in_1[0]);  // AND_Gate
endmodule

module SLA (
  input  [31:0] in_1,
  input  in_2,
  output [31:0] out_3
);

  \MUXÃO___32bits  \muxão_32bits_1  (.Canal_0(in_1), .Canal_1({in_1[30:0], in_1[0]}), .\Saída (out_3), .Seletor(in_2));
  Multiplexer #(.width(32), .enable("false")) multiplexer_1 ();  // open: in0, in1, out, sel

  // Notes on the sheet:
  //   Andar um bit para esquerda mantendo o sinal*
endmodule

module \SUBTRAÇÃO  (
  input  VEM_1,
  input  B,
  input  A,
  output \SUBTRAÇÃO ,
  output VAI_1
);

  wire and_1_out, and_2_out, and_3_out, xor_1_out;

  xor xor_1 (xor_1_out, B, A);
  and and_1 (and_1_out, ~A, VEM_1);  // AND_Gate
  and and_2 (and_2_out, B, VEM_1);
  and and_3 (and_3_out, ~A, B);  // AND_Gate
  xor xor_2 (\SUBTRAÇÃO , xor_1_out, VEM_1);
  or or_1 (VAI_1, and_1_out, and_2_out, and_3_out);
endmodule
