// Logisim project fase3-antigo.circ as structural Verilog
module main (
  input  [31:0] in_1,
  input  [31:0] in_2,
  input  [4:0] in_3,
  input  BNEGADO,
  output [31:0] out_5
);

  wire ula_32_1_overflow_soma;

  Hex_Digit_Display hex_digit_display_1 (.value(in_1[27:24]));  // open: dp
  Hex_Digit_Display hex_digit_display_2 (.value(in_1[31:28]));  // open: dp
  Hex_Digit_Display hex_digit_display_3 (.value(in_2[31:28]));  // open: dp
  Hex_Digit_Display hex_digit_display_4 (.value(in_2[27:24]));  // open: dp
  Hex_Digit_Display hex_digit_display_5 (.value(in_1[19:16]));  // open: dp
  Hex_Digit_Display hex_digit_display_6 (.value(in_1[23:20]));  // open: dp
  Hex_Digit_Display hex_digit_display_7 (.value(in_2[23:20]));  // open: dp
  Hex_Digit_Display hex_digit_display_8 (.value(in_2[19:16]));  // open: dp
  Hex_Digit_Display hex_digit_display_9 (.value(in_1[11:8]));  // open: dp
  Hex_Digit_Display hex_digit_display_10 (.value(in_1[15:12]));  // open: dp
  Hex_Digit_Display hex_digit_display_11 (.value(in_2[11:8]));  // open: dp
  Hex_Digit_Display hex_digit_display_12 (.value(in_2[15:12]));  // open: dp
  Hex_Digit_Display hex_digit_display_13 (.value(in_1[3:0]));  // open: dp
  Hex_Digit_Display hex_digit_display_14 (.value(in_1[7:4]));  // open: dp
  Hex_Digit_Display hex_digit_display_15 (.value(in_2[7:4]));  // open: dp
  Hex_Digit_Display hex_digit_display_16 (.value(in_2[3:0]));  // open: dp
  LED OVERFLOW_SOMA (.in(ula_32_1_overflow_soma));
  Hex_Digit_Display hex_digit_display_17 (.value(out_5[31:28]));  // open: dp
  ULA_32 ula_32_1 (.A(in_1), .B(in_2), .U(out_5), .\Operação (in_3), .OVERFLOW_SOMA(ula_32_1_overflow_soma));
  Hex_Digit_Display hex_digit_display_18 (.value(out_5[23:20]));  // open: dp
  Hex_Digit_Display hex_digit_display_19 (.value(out_5[27:24]));  // open: dp
  Hex_Digit_Display hex_digit_display_20 (.value(out_5[15:12]));  // open: dp
  Hex_Digit_Display hex_digit_display_21 (.value(out_5[19:16]));  // open: dp
  Hex_Digit_Display hex_digit_display_22 (.value(out_5[7:4]));  // open: dp
  Hex_Digit_Display hex_digit_display_23 (.value(out_5[11:8]));  // open: dp
  MENU menu_1 ();
  Hex_Digit_Display hex_digit_display_24 (.value(out_5[3:0]));  // open: dp
endmodule

module mux16 (
  input  Canal_0,
  input  Canal_1,
  input  Canal_2,
  input  Canal_3,
  input  Canal_4,
  input  Canal_5,
  input  Canal_6,
  input  Canal_7,
  input  Canal_8,
  input  Canal_9,
  input  Canal_10,
  input  Canal_11,
  input  Canal_12,
  input  Canal_13,
  input  Canal_14,
  input  Canal_15,
  input  SEL_3,
  input  SEL_2,
  input  SEL_1,
  input  SEL_0,
  output out_21
);

  wire mux8_1_saida, mux8_2_saida;

  mux8 mux8_1 (
    .Canal_0(Canal_0), .Canal_1(Canal_1), .Canal_2(Canal_2), .Canal_3(Canal_3), .Canal_4(Canal_4),
    .Canal_5(Canal_5), .Canal_6(Canal_6), .Canal_7(Canal_7), .Saida(mux8_1_saida), .Sel_2(SEL_2),
    .Sel_1(SEL_1), .Sel_0(SEL_0));
  mux8 mux8_2 (
    .Canal_0(Canal_8), .Canal_1(Canal_9), .Canal_2(Canal_10), .Canal_3(Canal_11), .Canal_4(Canal_12),
    .Canal_5(Canal_13), .Canal_6(Canal_14), .Canal_7(Canal_15), .Saida(mux8_2_saida), .Sel_2(SEL_2),
    .Sel_1(SEL_1), .Sel_0(SEL_0));
  mux2 mux2_1 (.Canal_0(mux8_1_saida), .Canal_1(mux8_2_saida), .out_4(out_21), .Seletor_0(SEL_3));
endmodule

module mux8 (
  input  Canal_0,
  input  Canal_1,
  input  Canal_2,
  input  Canal_3,
  input  Canal_4,
  input  Canal_5,
  input  Canal_6,
  input  Canal_7,
  input  Sel_2,
  input  Sel_1,
  input  Sel_0,
  output Saida
);

  wire and_1_out, and_2_out, and_3_out, and_4_out, and_5_out, and_6_out, and_7_out, and_8_out;

  and and_1 (and_1_out, Canal_0, ~Sel_2, ~Sel_1, ~Sel_0);  // AND_Gate
  and and_2 (and_2_out, Canal_1, ~Sel_2, ~Sel_1, Sel_0);  // AND_Gate
  and and_3 (and_3_out, Canal_2, ~Sel_2, Sel_1, ~Sel_0);  // AND_Gate
  and and_4 (and_4_out, Canal_3, ~Sel_2, Sel_1, Sel_0);  // AND_Gate
  and and_5 (and_5_out, Canal_4, Sel_2, ~Sel_1, ~Sel_0);  // AND_Gate
  and and_6 (and_6_out, Canal_5, Sel_2, ~Sel_1, Sel_0);  // AND_Gate
  and and_7 (and_7_out, Canal_6, Sel_2, Sel_1, ~Sel_0);  // AND_Gate
  and and_8 (and_8_out, Canal_7, Sel_2, Sel_1, Sel_0);
  or or_1 (Saida, and_1_out, and_2_out, and_3_out, and_4_out, and_5_out, and_6_out, and_7_out, and_8_out);
endmodule

module mux2 (
  input  Canal_0,
  input  Canal_1,
  input  Seletor_0,
  output out_4
);

  wire and_1_out, and_2_out;

  and and_1 (and_1_out, Canal_0, ~Seletor_0);  // AND_Gate
  and and_2 (and_2_out, Canal_1, Seletor_0);
  or or_1 (out_4, and_1_out, and_2_out);
endmodule

module ULA_1_BIT (
  input  A,
  input  B,
  input  VEM_1,
  input  Bnegado,
  input  [4:0] in_5,
  output U,
  output VAI_1
);

  wire and_1_out, mux2_1_out_4, nand_1_out, not_1_out, or_1_out, soma_1_soma, xor_1_out;

  not not_1 (not_1_out, B);
  mux2 mux2_1 (.Canal_0(B), .Canal_1(not_1_out), .out_4(mux2_1_out_4), .Seletor_0(Bnegado));
  and and_1 (and_1_out, A, B);
  or or_1 (or_1_out, A, B);
  xor xor_1 (xor_1_out, A, B);
  SOMA soma_1 (.SOMA(soma_1_soma), .VAI_1(VAI_1), .VEM_1(VEM_1), .B(mux2_1_out_4), .A(A));
  nand nand_1 (nand_1_out, A, B);
  mux32 mux32_1 (
    .out_38(U), .P(soma_1_soma), .Z6(A), .O(soma_1_soma), .J(nand_1_out), .H(B), .G(B), .F(B), .E(B),
    .C(xor_1_out), .B(or_1_out), .A(and_1_out), .SEL_0(in_5[0]), .SEL_1(in_5[1]), .SEL_2(in_5[2]),
    .SEL_3(in_5[3]), .SEL_4(in_5[4]));  // open: Z5, N, Z4, M, Z3, L, Z2, K, Z1, Z, I, Y, X, W, V, U, D, T, S, R, Q

  // Notes on the sheet:
  //   01111 = subtração com o vem 1 ativado
endmodule

module SOMA (
  input  VEM_1,
  input  B,
  input  A,
  output SOMA,
  output VAI_1
);

  wire and_1_out, and_2_out, and_3_out, xor_1_out;

  xor xor_1 (xor_1_out, B, A);
  and and_1 (and_1_out, A, VEM_1);
  and and_2 (and_2_out, B, VEM_1);
  and and_3 (and_3_out, A, B);
  xor xor_2 (SOMA, xor_1_out, VEM_1);
  or or_1 (VAI_1, and_1_out, and_2_out, and_3_out);
endmodule

module ULA_4BIT (
  input  [3:0] A,
  input  [3:0] B,
  input  [4:0] in_3,
  output [3:0] U,
  output OVERFLOW
);

  wire _0VAI1, _1VAI1, _2VAI1;

  ULA_1_BIT ula_1_bit_1 (.VAI_1(_0VAI1), .U(U[0]), .VEM_1(1'b0), .A(A[0]), .B(B[0]), .in_5(in_3));  // open: Bnegado
  ULA_1_BIT ula_1_bit_2 (.VAI_1(_1VAI1), .U(U[1]), .VEM_1(_0VAI1), .A(A[1]), .B(B[1]), .in_5(in_3));  // open: Bnegado
  ULA_1_BIT ula_1_bit_3 (.VAI_1(_2VAI1), .U(U[2]), .VEM_1(_1VAI1), .A(A[2]), .B(B[2]), .in_5(in_3));  // open: Bnegado
  ULA_1_BIT ula_1_bit_4 (.VAI_1(OVERFLOW), .U(U[3]), .VEM_1(_2VAI1), .A(A[3]), .B(B[3]), .in_5(in_3));  // open: Bnegado

  // Other names for the same wires on the sheet: SELETOR[4:0] = in_3

  // Notes on the sheet:
  //   000 = AND
  //   001 = OR
  //   010 = XOR
  //   011 = SOMA
endmodule

module ULA_32 (
  input  [31:0] A,
  input  [31:0] B,
  input  [4:0] \Operação ,
  output OVERFLOW_SOMA,
  output [31:0] U
);

  wire _0VAI1, _1VAI1, _2VAI1, _3VAI1, _4VAI1, _5VAI1, _6VAI1, _7VAI1, _8VAI1, _9VAI1, _10VAI1, _11VAI1,
       _12VAI1, _13VAI1, _14VAI1, _15VAI1, _16VAI1, _17VAI1, _18VAI1, _19VAI1, _20VAI1, _21VAI1, _22VAI1,
       _23VAI1, _24VAI1, _25VAI1, _26VAI1, _27VAI1, _28VAI1, _29VAI1, _30VAI1, A0, A1, A2, A3, A4, A5, A6,
       A7, A8, A9, A10, A11, A12, A13, A14, A15, A16, A17, A18, A19, A20, A21, A22, A23, A24, A25, A26, A27,
       A28, A29, A30, A31, B0, B1, B2, B3, B4, B5, B6, B7, B8, B9, B10, B11, B12, B13, B14, B15, B16, B17,
       B18, B19, B20, B21, B22, B23, B24, B25, B26, B27, B28, B29, B30, B31, lua_detect_1_out_2,
       sla_detect_1_out_2, sll_detect_1_out_2, sra_detect_1_out_2, srl_detect_1_out_2,
       \subtração_detect_1_out_2 ;
  wire [31:0] sll_1_out_3, sra_1_out_3, srl_1_out_3;

  lua_detect lua_detect_1 (.out_2(lua_detect_1_out_2), .in_1(\Operação ));
  ULA_1_BIT ula_1_bit_1 (
    .VAI_1(_9VAI1), .U(U[9]), .VEM_1(_8VAI1), .A(A9), .B(B9), .in_5(\Operação ),
    .Bnegado(\subtração_detect_1_out_2 ));
  ULA_1_BIT ula_1_bit_2 (
    .VAI_1(_19VAI1), .U(U[19]), .VEM_1(_18VAI1), .A(A19), .B(B19), .in_5(\Operação ),
    .Bnegado(\subtração_detect_1_out_2 ));
  ULA_1_BIT ula_1_bit_3 (
    .VAI_1(_29VAI1), .U(U[29]), .VEM_1(_28VAI1), .A(A29), .B(B19), .in_5(\Operação ),
    .Bnegado(\subtração_detect_1_out_2 ));
  lua lua_1 (
    .valor(A), .seletor(lua_detect_1_out_2),
    .saida({A31, A30, A29, A28, A27, A26, A25, A24, A23, A22, A21, A20, A19, A18, A17, A16, A15, A14, A13, A12, A11, A10, A9, A8, A7, A6, A5, A4, A3, A2, A1, A0}));
  ULA_1_BIT ula_1_bit_4 (
    .VAI_1(_8VAI1), .U(U[8]), .VEM_1(_7VAI1), .A(A8), .B(B8), .in_5(\Operação ),
    .Bnegado(\subtração_detect_1_out_2 ));
  ULA_1_BIT ula_1_bit_5 (
    .VAI_1(_18VAI1), .U(U[18]), .VEM_1(_17VAI1), .A(A18), .B(B18), .in_5(\Operação ),
    .Bnegado(\subtração_detect_1_out_2 ));
  ULA_1_BIT ula_1_bit_6 (
    .VAI_1(_28VAI1), .U(U[28]), .VEM_1(_27VAI1), .A(A28), .B(B28), .in_5(\Operação ),
    .Bnegado(\subtração_detect_1_out_2 ));
  ULA_1_BIT ula_1_bit_7 (
    .VAI_1(_7VAI1), .U(U[7]), .VEM_1(_6VAI1), .A(A7), .B(B7), .in_5(\Operação ),
    .Bnegado(\subtração_detect_1_out_2 ));
  ULA_1_BIT ula_1_bit_8 (
    .VAI_1(_17VAI1), .U(U[17]), .VEM_1(_16VAI1), .A(A17), .B(B17), .in_5(\Operação ),
    .Bnegado(\subtração_detect_1_out_2 ));
  ULA_1_BIT ula_1_bit_9 (
    .VAI_1(_27VAI1), .U(U[27]), .VEM_1(_26VAI1), .A(A27), .B(B27), .in_5(\Operação ),
    .Bnegado(\subtração_detect_1_out_2 ));
  ULA_1_BIT ula_1_bit_10 (
    .VAI_1(_6VAI1), .U(U[6]), .VEM_1(_5VAI1), .A(A6), .B(B6), .in_5(\Operação ),
    .Bnegado(\subtração_detect_1_out_2 ));
  ULA_1_BIT ula_1_bit_11 (
    .VAI_1(_16VAI1), .U(U[16]), .VEM_1(_15VAI1), .A(A16), .B(B16), .in_5(\Operação ),
    .Bnegado(\subtração_detect_1_out_2 ));
  ULA_1_BIT ula_1_bit_12 (
    .VAI_1(_26VAI1), .U(U[26]), .VEM_1(_25VAI1), .A(A26), .B(B26), .in_5(\Operação ),
    .Bnegado(\subtração_detect_1_out_2 ));
  SRL srl_1 (.in_1(sll_1_out_3), .in_2(srl_detect_1_out_2), .out_3(srl_1_out_3));
  SLL sll_1 (.in_1(B), .in_2(sll_detect_1_out_2), .out_3(sll_1_out_3));
  SLL_Detect sll_detect_1 (.out_2(sll_detect_1_out_2), .in_1(\Operação ));
  SRL_Detect srl_detect_1 (.out_2(srl_detect_1_out_2), .in_1(\Operação ));
  SRA sra_1 (.in_1(srl_1_out_3), .in_2(sra_detect_1_out_2), .out_3(sra_1_out_3));
  SLA_DETECT sla_detect_1 (.out_2(sla_detect_1_out_2), .in_1(\Operação ));
  SRA_Detect sra_detect_1 (.out_2(sra_detect_1_out_2), .in_1(\Operação ));
  ULA_1_BIT ula_1_bit_13 (
    .VAI_1(_5VAI1), .U(U[5]), .VEM_1(_4VAI1), .A(A5), .B(B5), .in_5(\Operação ),
    .Bnegado(\subtração_detect_1_out_2 ));
  ULA_1_BIT ula_1_bit_14 (
    .VAI_1(_15VAI1), .U(U[15]), .VEM_1(_14VAI1), .A(A15), .B(B15), .in_5(\Operação ),
    .Bnegado(\subtração_detect_1_out_2 ));
  ULA_1_BIT ula_1_bit_15 (
    .VAI_1(_25VAI1), .U(U[25]), .VEM_1(_24VAI1), .A(A25), .B(B25), .in_5(\Operação ),
    .Bnegado(\subtração_detect_1_out_2 ));
  SLA sla_1 (
    .in_1(sra_1_out_3), .in_2(sla_detect_1_out_2),
    .out_3({B31, B30, B29, B28, B27, B26, B25, B24, B23, B22, B21, B20, B19, B18, B17, B16, B15, B14, B13, B12, B11, B10, B9, B8, B7, B6, B5, B4, B3, B2, B1, B0}));
  ULA_1_BIT ula_1_bit_16 (
    .VAI_1(_4VAI1), .U(U[4]), .VEM_1(_3VAI1), .A(A4), .B(B4), .in_5(\Operação ),
    .Bnegado(\subtração_detect_1_out_2 ));
  ULA_1_BIT ula_1_bit_17 (
    .VAI_1(_14VAI1), .U(U[14]), .VEM_1(_13VAI1), .A(A14), .B(B14), .in_5(\Operação ),
    .Bnegado(\subtração_detect_1_out_2 ));
  ULA_1_BIT ula_1_bit_18 (
    .VAI_1(_24VAI1), .U(U[24]), .VEM_1(_23VAI1), .A(A24), .B(B24), .in_5(\Operação ),
    .Bnegado(\subtração_detect_1_out_2 ));
  ULA_1_BIT ula_1_bit_19 (
    .VAI_1(_3VAI1), .U(U[3]), .VEM_1(_2VAI1), .A(A3), .B(B3), .in_5(\Operação ),
    .Bnegado(\subtração_detect_1_out_2 ));
  ULA_1_BIT ula_1_bit_20 (
    .VAI_1(_13VAI1), .U(U[13]), .VEM_1(_12VAI1), .A(A13), .B(B13), .in_5(\Operação ),
    .Bnegado(\subtração_detect_1_out_2 ));
  ULA_1_BIT ula_1_bit_21 (
    .VAI_1(_23VAI1), .U(U[23]), .VEM_1(_22VAI1), .A(A23), .B(B23), .in_5(\Operação ),
    .Bnegado(\subtração_detect_1_out_2 ));
  ULA_1_BIT ula_1_bit_22 (
    .VAI_1(_2VAI1), .U(U[2]), .VEM_1(_1VAI1), .A(A2), .B(B2), .in_5(\Operação ),
    .Bnegado(\subtração_detect_1_out_2 ));
  ULA_1_BIT ula_1_bit_23 (
    .VAI_1(_12VAI1), .U(U[12]), .VEM_1(_11VAI1), .A(A12), .B(B12), .in_5(\Operação ),
    .Bnegado(\subtração_detect_1_out_2 ));
  ULA_1_BIT ula_1_bit_24 (
    .VAI_1(_22VAI1), .U(U[22]), .VEM_1(_21VAI1), .A(A22), .B(B22), .in_5(\Operação ),
    .Bnegado(\subtração_detect_1_out_2 ));
  ULA_1_BIT ula_1_bit_25 (
    .VAI_1(_1VAI1), .U(U[1]), .VEM_1(_0VAI1), .A(A1), .B(B1), .in_5(\Operação ),
    .Bnegado(\subtração_detect_1_out_2 ));
  ULA_1_BIT ula_1_bit_26 (
    .VAI_1(_11VAI1), .U(U[11]), .VEM_1(_10VAI1), .A(A11), .B(B11), .in_5(\Operação ),
    .Bnegado(\subtração_detect_1_out_2 ));
  ULA_1_BIT ula_1_bit_27 (
    .VAI_1(_21VAI1), .U(U[21]), .VEM_1(_20VAI1), .A(A21), .B(B21), .in_5(\Operação ),
    .Bnegado(\subtração_detect_1_out_2 ));
  ULA_1_BIT ula_1_bit_28 (
    .VAI_1(OVERFLOW_SOMA), .U(U[31]), .VEM_1(_30VAI1), .A(A31), .B(B31), .in_5(\Operação ),
    .Bnegado(\subtração_detect_1_out_2 ));
  MENU menu_1 ();
  ULA_1_BIT ula_1_bit_29 (
    .VAI_1(_30VAI1), .U(U[30]), .VEM_1(_29VAI1), .A(A30), .B(B30), .in_5(\Operação ),
    .Bnegado(\subtração_detect_1_out_2 ));
  ULA_1_BIT ula_1_bit_30 (
    .VAI_1(_0VAI1), .U(U[0]), .VEM_1(\subtração_detect_1_out_2 ), .A(A0), .B(B0), .in_5(\Operação ),
    .Bnegado(\subtração_detect_1_out_2 ));
  ULA_1_BIT ula_1_bit_31 (
    .VAI_1(_10VAI1), .U(U[10]), .VEM_1(_9VAI1), .A(A10), .B(B10), .in_5(\Operação ),
    .Bnegado(\subtração_detect_1_out_2 ));
  ULA_1_BIT ula_1_bit_32 (
    .VAI_1(_20VAI1), .U(U[20]), .VEM_1(_19VAI1), .A(A20), .B(B20), .in_5(\Operação ),
    .Bnegado(\subtração_detect_1_out_2 ));
  \SUBTRAÇÃO_DETECT  \subtração_detect_1  (.out_2(\subtração_detect_1_out_2 ), .in_1(\Operação ));

  // Other names for the same wires on the sheet: _31VAI1 = OVERFLOW_SOMA
endmodule

module mux32 (
  input  P,
  input  O,
  input  N,
  input  M,
  input  L,
  input  K,
  input  J,
  input  I,
  input  H,
  input  G,
  input  F,
  input  E,
  input  D,
  input  C,
  input  B,
  input  A,
  input  Z6,
  input  Z5,
  input  Z4,
  input  Z3,
  input  Z2,
  input  Z1,
  input  Z,
  input  Y,
  input  X,
  input  W,
  input  V,
  input  U,
  input  T,
  input  S,
  input  R,
  input  Q,
  input  SEL_4,
  input  SEL_3,
  input  SEL_2,
  input  SEL_1,
  input  SEL_0,
  output out_38
);

  wire mux16_1_out_21, mux16_2_out_21;

  mux16 mux16_1 (
    .out_21(mux16_1_out_21), .Canal_0(A), .Canal_1(B), .Canal_2(C), .Canal_3(D), .Canal_4(E), .Canal_5(F),
    .Canal_6(G), .Canal_7(H), .Canal_8(I), .Canal_9(J), .Canal_10(K), .Canal_11(L), .Canal_12(M),
    .Canal_13(N), .Canal_14(O), .Canal_15(P), .SEL_0(SEL_0), .SEL_1(SEL_1), .SEL_2(SEL_2), .SEL_3(SEL_3));
  mux16 mux16_2 (
    .out_21(mux16_2_out_21), .Canal_0(Q), .Canal_1(R), .Canal_2(S), .Canal_3(T), .Canal_4(U), .Canal_5(V),
    .Canal_6(W), .Canal_7(X), .Canal_8(Y), .Canal_9(Z), .Canal_10(Z1), .Canal_11(Z2), .Canal_12(Z3),
    .Canal_13(Z4), .Canal_14(Z5), .Canal_15(Z6), .SEL_0(SEL_0), .SEL_1(SEL_1), .SEL_2(SEL_2), .SEL_3(SEL_3));
  mux2 mux2_1 (.Canal_0(mux16_1_out_21), .Canal_1(mux16_2_out_21), .out_4(out_38), .Seletor_0(SEL_4));
endmodule

module SLL (
  input  [31:0] in_1,
  input  in_2,
  output [31:0] out_3
);

  \MUXÃO___32bits  \muxão_32bits_1  (.Canal_0(in_1), .Canal_1({in_1[30:0], 1'b0}), .\Saída (out_3), .Seletor(in_2));
  Multiplexer #(.width(32), .enable("false")) multiplexer_1 ();  // open: in0, in1, out, sel

  // Notes on the sheet:
  //   Andar um bit para esquerda
endmodule

module SRL (
  input  [31:0] in_1,
  input  in_2,
  output [31:0] out_3
);

  \MUXÃO___32bits  \muxão_32bits_1  (.Canal_0(in_1), .Canal_1({1'b0, in_1[31:1]}), .\Saída (out_3), .Seletor(in_2));
  Multiplexer #(.width(32), .enable("false")) multiplexer_1 ();  // open: in0, in1, out, sel

  // Notes on the sheet:
  //   Andar um bit para direita
endmodule

module SRA (
  input  [31:0] in_1,
  input  in_2,
  output [31:0] out_3
);

  \MUXÃO___32bits  \muxão_32bits_1  (
    .Canal_0(in_1), .Canal_1({{2{in_1[31]}}, in_1[30:1]}), .\Saída (out_3), .Seletor(in_2));
  Multiplexer #(.width(32), .enable("false")) multiplexer_1 ();  // open: in0, in1, out, sel

  // Notes on the sheet:
  //   Andar um bit para direita mantendo o sinal
endmodule

// SLLD
module SLL_Detect (
  input  [4:0] in_1,
  output out_2
);

  and and_1 (out_2, ~in_1[4], ~in_1[3], in_1[2], ~in_1[1], ~in_1[0]);  // AND_Gate
endmodule

// SRLD
module SRL_Detect (
  input  [4:0] in_1,
  output out_2
);

  and and_1 (out_2, ~in_1[4], ~in_1[3], in_1[2], ~in_1[1], in_1[0]);  // AND_Gate
endmodule

// SRAD
module SRA_Detect (
  input  [4:0] in_1,
  output out_2
);

  and and_1 (out_2, ~in_1[4], ~in_1[3], in_1[2], in_1[1], ~in_1[0]);  // AND_Gate
endmodule

module \MUXÃO___32bits  (
  input  Seletor,
  input  [31:0] Canal_0,
  input  [31:0] Canal_1,
  output [31:0] \Saída 
);

  mux2 mux2_1 (.Canal_0(Canal_0[15]), .Canal_1(Canal_1[15]), .out_4(\Saída [15]), .Seletor_0(Seletor));
  mux2 mux2_2 (.Canal_0(Canal_0[16]), .Canal_1(Canal_1[16]), .out_4(\Saída [16]), .Seletor_0(Seletor));
  mux2 mux2_3 (.Canal_0(Canal_0[14]), .Canal_1(Canal_1[14]), .out_4(\Saída [14]), .Seletor_0(Seletor));
  mux2 mux2_4 (.Canal_0(Canal_0[17]), .Canal_1(Canal_1[17]), .out_4(\Saída [17]), .Seletor_0(Seletor));
  mux2 mux2_5 (.Canal_0(Canal_0[13]), .Canal_1(Canal_1[13]), .out_4(\Saída [13]), .Seletor_0(Seletor));
  mux2 mux2_6 (.Canal_0(Canal_0[18]), .Canal_1(Canal_1[18]), .out_4(\Saída [18]), .Seletor_0(Seletor));
  mux2 mux2_7 (.Canal_0(Canal_0[12]), .Canal_1(Canal_1[12]), .out_4(\Saída [12]), .Seletor_0(Seletor));
  mux2 mux2_8 (.Canal_0(Canal_0[19]), .Canal_1(Canal_1[19]), .out_4(\Saída [19]), .Seletor_0(Seletor));
  mux2 mux2_9 (.Canal_0(Canal_0[11]), .Canal_1(Canal_1[11]), .out_4(\Saída [11]), .Seletor_0(Seletor));
  mux2 mux2_10 (.Canal_0(Canal_0[20]), .Canal_1(Canal_1[20]), .out_4(\Saída [20]), .Seletor_0(Seletor));
  mux2 mux2_11 (.Canal_0(Canal_0[10]), .Canal_1(Canal_1[10]), .out_4(\Saída [10]), .Seletor_0(Seletor));
  mux2 mux2_12 (.Canal_0(Canal_0[21]), .Canal_1(Canal_1[21]), .out_4(\Saída [21]), .Seletor_0(Seletor));
  mux2 mux2_13 (.Canal_0(Canal_0[9]), .Canal_1(Canal_1[9]), .out_4(\Saída [9]), .Seletor_0(Seletor));
  mux2 mux2_14 (.Canal_0(Canal_0[22]), .Canal_1(Canal_1[22]), .out_4(\Saída [22]), .Seletor_0(Seletor));
  mux2 mux2_15 (.Canal_0(Canal_0[8]), .Canal_1(Canal_1[8]), .out_4(\Saída [8]), .Seletor_0(Seletor));
  mux2 mux2_16 (.Canal_0(Canal_0[23]), .Canal_1(Canal_1[23]), .out_4(\Saída [23]), .Seletor_0(Seletor));
  mux2 mux2_17 (.Canal_0(Canal_0[7]), .Canal_1(Canal_1[7]), .out_4(\Saída [7]), .Seletor_0(Seletor));
  mux2 mux2_18 (.Canal_0(Canal_0[24]), .Canal_1(Canal_1[24]), .out_4(\Saída [24]), .Seletor_0(Seletor));
  mux2 mux2_19 (.Canal_0(Canal_0[6]), .Canal_1(Canal_1[6]), .out_4(\Saída [6]), .Seletor_0(Seletor));
  mux2 mux2_20 (.Canal_0(Canal_0[25]), .Canal_1(Canal_1[25]), .out_4(\Saída [25]), .Seletor_0(Seletor));
  mux2 mux2_21 (.Canal_0(Canal_0[5]), .Canal_1(Canal_1[5]), .out_4(\Saída [5]), .Seletor_0(Seletor));
  mux2 mux2_22 (.Canal_0(Canal_0[26]), .Canal_1(Canal_1[26]), .out_4(\Saída [26]), .Seletor_0(Seletor));
  mux2 mux2_23 (.Canal_0(Canal_0[4]), .Canal_1(Canal_1[4]), .out_4(\Saída [4]), .Seletor_0(Seletor));
  mux2 mux2_24 (.Canal_0(Canal_0[27]), .Canal_1(Canal_1[27]), .out_4(\Saída [27]), .Seletor_0(Seletor));
  mux2 mux2_25 (.Canal_0(Canal_0[3]), .Canal_1(Canal_1[3]), .out_4(\Saída [3]), .Seletor_0(Seletor));
  mux2 mux2_26 (.Canal_0(Canal_0[28]), .Canal_1(Canal_1[28]), .out_4(\Saída [28]), .Seletor_0(Seletor));
  mux2 mux2_27 (.Canal_0(Canal_0[2]), .Canal_1(Canal_1[2]), .out_4(\Saída [2]), .Seletor_0(Seletor));
  mux2 mux2_28 (.Canal_0(Canal_0[29]), .Canal_1(Canal_1[29]), .out_4(\Saída [29]), .Seletor_0(Seletor));
  mux2 mux2_29 (.Canal_0(Canal_0[1]), .Canal_1(Canal_1[1]), .out_4(\Saída [1]), .Seletor_0(Seletor));
  mux2 mux2_30 (.Canal_0(Canal_0[30]), .Canal_1(Canal_1[30]), .out_4(\Saída [30]), .Seletor_0(Seletor));
  mux2 mux2_31 (.Canal_0(Canal_0[0]), .Canal_1(Canal_1[0]), .out_4(\Saída [0]), .Seletor_0(Seletor));
  mux2 mux2_32 (.Canal_0(Canal_0[31]), .Canal_1(Canal_1[31]), .out_4(\Saída [31]), .Seletor_0(Seletor));

  // Other names for the same wires on the sheet: A0 = Canal_0[0]; A1 = Canal_0[1]; A2 = Canal_0[2]; A3 = Canal_0[3];
  //   A4 = Canal_0[4]; A5 = Canal_0[5]; A6 = Canal_0[6]; A7 = Canal_0[7]; A8 = Canal_0[8]; A9 = Canal_0[9];
  //   A10 = Canal_0[10]; A11 = Canal_0[11]; A12 = Canal_0[12]; A13 = Canal_0[13]; A14 = Canal_0[14];
  //   A15 = Canal_0[15]; A16 = Canal_0[16]; A17 = Canal_0[17]; A18 = Canal_0[18]; A19 = Canal_0[19];
  //   A20 = Canal_0[20]; A21 = Canal_0[21]; A22 = Canal_0[22]; A23 = Canal_0[23]; A24 = Canal_0[24];
  //   A25 = Canal_0[25]; A26 = Canal_0[26]; A27 = Canal_0[27]; A28 = Canal_0[28]; A29 = Canal_0[29];
  //   A30 = Canal_0[30]; A31 = Canal_0[31]; B0 = Canal_1[0]; B1 = Canal_1[1]; B2 = Canal_1[2]; B3 = Canal_1[3];
  //   B4 = Canal_1[4]; B5 = Canal_1[5]; B6 = Canal_1[6]; B7 = Canal_1[7]; B8 = Canal_1[8]; B9 = Canal_1[9];
  //   B10 = Canal_1[10]; B11 = Canal_1[11]; B12 = Canal_1[12]; B13 = Canal_1[13]; B14 = Canal_1[14];
  //   B15 = Canal_1[15]; B16 = Canal_1[16]; B17 = Canal_1[17]; B18 = Canal_1[18]; B19 = Canal_1[19];
  //   B20 = Canal_1[20]; B21 = Canal_1[21]; B22 = Canal_1[22]; B23 = Canal_1[23]; B24 = Canal_1[24];
  //   B25 = Canal_1[25]; B26 = Canal_1[26]; B27 = Canal_1[27]; B28 = Canal_1[28]; B29 = Canal_1[29];
  //   B30 = Canal_1[30]; B31 = Canal_1[31]; S0 = \Saída [0]; S1 = \Saída [1]; S2 = \Saída [2]; S3 = \Saída [3];
  //   S4 = \Saída [4]; S5 = \Saída [5]; S6 = \Saída [6]; S7 = \Saída [7]; S8 = \Saída [8]; S9 = \Saída [9];
  //   S10 = \Saída [10]; S11 = \Saída [11]; S12 = \Saída [12]; S13 = \Saída [13]; S14 = \Saída [14];
  //   S15 = \Saída [15]; S16 = \Saída [16]; S17 = \Saída [17]; S18 = \Saída [18]; S19 = \Saída [19];
  //   S20 = \Saída [20]; S21 = \Saída [21]; S22 = \Saída [22]; S23 = \Saída [23]; S24 = \Saída [24];
  //   S25 = \Saída [25]; S26 = \Saída [26]; S27 = \Saída [27]; S28 = \Saída [28]; S29 = \Saída [29];
  //   S30 = \Saída [30]; S31 = \Saída [31]
endmodule

// SLAD
module SLA_DETECT (
  input  [4:0] in_1,
  output out_2
);

  and and_1 (out_2, ~in_1[4], ~in_1[3], in_1[2], in_1[1], in_1[0]);  // AND_Gate
endmodule

module SLA (
  input  [31:0] in_1,
  input  in_2,
  output [31:0] out_3
);

  \MUXÃO___32bits  \muxão_32bits_1  (.Canal_0(in_1), .Canal_1({in_1[30:0], in_1[0]}), .\Saída (out_3), .Seletor(in_2));
  Multiplexer #(.width(32), .enable("false")) multiplexer_1 ();  // open: in0, in1, out, sel

  // Notes on the sheet:
  //   Andar um bit para esquerda mantendo o sinal*
endmodule

module \SUBTRAÇÃO  (
  input  VEM_1,
  input  B,
  input  A,
  output \SUBTRAÇÃO ,
  output VAI_1
);

  wire and_1_out, and_2_out, and_3_out, xor_1_out;

  xor xor_1 (xor_1_out, B, A);
  and and_1 (and_1_out, ~A, VEM_1);  // AND_Gate
  and and_2 (and_2_out, B, VEM_1);
  and and_3 (and_3_out, ~A, B);  // AND_Gate
  xor xor_2 (\SUBTRAÇÃO , xor_1_out, VEM_1);
  or or_1 (VAI_1, and_1_out, and_2_out, and_3_out);
endmodule

module lua (
  input  [31:0] valor,
  input  seletor,
  output [31:0] saida
);

  \MUXÃO___32bits  \muxão_32bits_1  (
    .Canal_0(valor), .Canal_1({valor[15:0], {16{1'b0}}}), .\Saída (saida), .Seletor(seletor));
endmodule

module lua_detect (
  input  [4:0] in_1,
  output out_2
);

  and and_1 (out_2, in_1[4], in_1[3], in_1[2], in_1[1], in_1[0]);
endmodule

module \SUBTRAÇÃO_DETECT  (
  input  [4:0] in_1,
  output out_2
);

  and and_1 (out_2, ~in_1[4], in_1[3], in_1[2], in_1[1], in_1[0]);  // AND_Gate
endmodule

// Reg
module Registrador (
  input  [31:0] Input,
  input  RESET,
  input  CLK,
  output [31:0] Output
);

  D_Flip_Flop d_ff_1 (.clk(CLK), .D(Input[31]), .Q(Output[31]), .reset(RESET));  // open: Qn, preset, en
  D_Flip_Flop d_ff_2 (.clk(CLK), .D(Input[15]), .Q(Output[15]), .reset(RESET));  // open: Qn, preset, en
  D_Flip_Flop d_ff_3 (.clk(CLK), .D(Input[30]), .Q(Output[30]), .reset(RESET));  // open: Qn, preset, en
  D_Flip_Flop d_ff_4 (.clk(CLK), .D(Input[14]), .Q(Output[14]), .reset(RESET));  // open: Qn, preset, en
  D_Flip_Flop d_ff_5 (.clk(CLK), .D(Input[29]), .Q(Output[29]), .reset(RESET));  // open: Qn, preset, en
  D_Flip_Flop d_ff_6 (.clk(CLK), .D(Input[13]), .Q(Output[13]), .reset(RESET));  // open: Qn, preset, en
  D_Flip_Flop d_ff_7 (.clk(CLK), .D(Input[28]), .Q(Output[28]), .reset(RESET));  // open: Qn, preset, en
  D_Flip_Flop d_ff_8 (.clk(CLK), .D(Input[12]), .Q(Output[12]), .reset(RESET));  // open: Qn, preset, en
  D_Flip_Flop d_ff_9 (.clk(CLK), .D(Input[27]), .Q(Output[27]), .reset(RESET));  // open: Qn, preset, en
  D_Flip_Flop d_ff_10 (.clk(CLK), .D(Input[11]), .Q(Output[11]), .reset(RESET));  // open: Qn, preset, en
  D_Flip_Flop d_ff_11 (.clk(CLK), .D(Input[26]), .Q(Output[26]), .reset(RESET));  // open: Qn, preset, en
  D_Flip_Flop d_ff_12 (.clk(CLK), .D(Input[10]), .Q(Output[10]), .reset(RESET));  // open: Qn, preset, en
  D_Flip_Flop d_ff_13 (.clk(CLK), .D(Input[25]), .Q(Output[25]), .reset(RESET));  // open: Qn, preset, en
  D_Flip_Flop d_ff_14 (.clk(CLK), .D(Input[9]), .Q(Output[9]), .reset(RESET));  // open: Qn, preset, en
  D_Flip_Flop d_ff_15 (.clk(CLK), .D(Input[24]), .Q(Output[24]), .reset(RESET));  // open: Qn, preset, en
  D_Flip_Flop d_ff_16 (.clk(CLK), .D(Input[8]), .Q(Output[8]), .reset(RESET));  // open: Qn, preset, en
  D_Flip_Flop d_ff_17 (.clk(CLK), .D(Input[23]), .Q(Output[23]), .reset(RESET));  // open: Qn, preset, en
  D_Flip_Flop d_ff_18 (.clk(CLK), .D(Input[7]), .Q(Output[7]), .reset(RESET));  // open: Qn, preset, en
  D_Flip_Flop d_ff_19 (.clk(CLK), .D(Input[22]), .Q(Output[22]), .reset(RESET));  // open: Qn, preset, en
  D_Flip_Flop d_ff_20 (.clk(CLK), .D(Input[6]), .Q(Output[6]), .reset(RESET));  // open: Qn, preset, en
  D_Flip_Flop d_ff_21 (.clk(CLK), .D(Input[21]), .Q(Output[21]), .reset(RESET));  // open: Qn, preset, en
  D_Flip_Flop d_ff_22 (.clk(CLK), .D(Input[5]), .Q(Output[5]), .reset(RESET));  // open: Qn, preset, en
  D_Flip_Flop d_ff_23 (.clk(CLK), .D(Input[20]), .Q(Output[20]), .reset(RESET));  // open: Qn, preset, en
  D_Flip_Flop d_ff_24 (.clk(CLK), .D(Input[4]), .Q(Output[4]), .reset(RESET));  // open: Qn, preset, en
  D_Flip_Flop d_ff_25 (.clk(CLK), .D(Input[19]), .Q(Output[19]), .reset(RESET));  // open: Qn, preset, en
  D_Flip_Flop d_ff_26 (.clk(CLK), .D(Input[3]), .Q(Output[3]), .reset(RESET));  // open: Qn, preset, en
  D_Flip_Flop d_ff_27 (.clk(CLK), .D(Input[18]), .Q(Output[18]), .reset(RESET));  // open: Qn, preset, en
  D_Flip_Flop d_ff_28 (.clk(CLK), .D(Input[2]), .Q(Output[2]), .reset(RESET));  // open: Qn, preset, en
  D_Flip_Flop d_ff_29 (.clk(CLK), .D(Input[17]), .Q(Output[17]), .reset(RESET));  // open: Qn, preset, en
  D_Flip_Flop d_ff_30 (.clk(CLK), .D(Input[1]), .Q(Output[1]), .reset(RESET));  // open: Qn, preset, en
  D_Flip_Flop d_ff_31 (.clk(CLK), .D(Input[16]), .Q(Output[16]), .reset(RESET));  // open: Qn, preset, en
  D_Flip_Flop d_ff_32 (.clk(CLK), .D(Input[0]), .Q(Output[0]), .reset(RESET));  // open: Qn, preset, en

  // Other names for the same wires on the sheet: i0 = Input[0]; i1 = Input[1]; i2 = Input[2]; i3 = Input[3];
  //   i4 = Input[4]; i5 = Input[5]; i6 = Input[6]; i7 = Input[7]; i8 = Input[8]; i9 = Input[9]; i10 = Input[10];
  //   i11 = Input[11]; i12 = Input[12]; i13 = Input[13]; i14 = Input[14]; i15 = Input[15]; i16 = Input[16];
  //   i17 = Input[17]; i18 = Input[18]; i19 = Input[19]; i20 = Input[20]; i21 = Input[21]; i22 = Input[22];
  //   i23 = Input[23]; i24 = Input[24]; i25 = Input[25]; i26 = Input[26]; i27 = Input[27]; i28 = Input[28];
  //   i29 = Input[29]; i30 = Input[30]; i31 = Input[31]; o0 = Output[0]; o1 = Output[1]; o2 = Output[2];
  //   o3 = Output[3]; o4 = Output[4]; o5 = Output[5]; o6 = Output[6]; o7 = Output[7]; o8 = Output[8]; o9 = Output[9];
  //   o10 = Output[10]; o11 = Output[11]; o12 = Output[12]; o13 = Output[13]; o14 = Output[14]; o15 = Output[15];
  //   o16 = Output[16]; o17 = Output[17]; o18 = Output[18]; o19 = Output[19]; o20 = Output[20]; o21 = Output[21];
  //   o22 = Output[22]; o23 = Output[23]; o24 = Output[24]; o25 = Output[25]; o26 = Output[26]; o27 = Output[27];
  //   o28 = Output[28]; o29 = Output[29]; o30 = Output[30]; o31 = Output[31]
endmodule

module Banco_de_Registradores (
  input  Reset,
  input  [31:0] Entrada_de_Dados,
  input  CLK,
  input  [4:0] Seletor_Registrador_A,
  input  [4:0] in_5,
  input  [4:0] Seletor_Registrador_B,
  output [31:0] Dados_Registrador_A,
  output [31:0] Dados_Registrador_B
);

  wire CLK1, CLK2, CLK3, CLK4, CLK5, CLK6, CLK7, CLK8, CLK9, CLK10, CLK11, CLK12, CLK13, CLK14, CLK15, CLK16,
       CLK17, CLK18, CLK19, CLK20, CLK21, CLK22, CLK23, CLK24, CLK25, CLK26, CLK27, CLK28, CLK29, CLK30,
       CLK31, demultiplexer_1_out0;
  wire [31:0] out1, out2, out3, out4, out5, out6, out7, out8, out9, out10, out11, out12, out13, out14, out15,
       out16, out17, out18, out19, out20, out21, out22, out23, out24, out25, out26, out27, out28, out29,
       out30, out31;

  Demultiplexer #(.select(5), .enable("false")) demultiplexer_1 (
    .out0(demultiplexer_1_out0), .out1(CLK1), .out2(CLK2), .out3(CLK3), .out4(CLK4), .out5(CLK5),
    .out6(CLK6), .out7(CLK7), .out8(CLK8), .out9(CLK9), .out10(CLK10), .out11(CLK11), .out12(CLK12),
    .out13(CLK13), .out14(CLK14), .out15(CLK15), .out16(CLK16), .out17(CLK17), .out18(CLK18), .out19(CLK19),
    .out20(CLK20), .out21(CLK21), .out22(CLK22), .out23(CLK23), .out24(CLK24), .out25(CLK25), .out26(CLK26),
    .out27(CLK27), .out28(CLK28), .out29(CLK29), .out30(CLK30), .out31(CLK31), .in(CLK), .sel(in_5));
  Registrador _1 (.CLK(CLK1), .RESET(Reset), .Input(Entrada_de_Dados), .Output(out1));
  Registrador _2 (.CLK(CLK2), .RESET(Reset), .Input(Entrada_de_Dados), .Output(out2));
  Registrador _3 (.CLK(CLK3), .RESET(Reset), .Input(Entrada_de_Dados), .Output(out3));
  Registrador _4 (.CLK(CLK4), .RESET(Reset), .Input(Entrada_de_Dados), .Output(out4));
  Registrador _5 (.CLK(CLK5), .RESET(Reset), .Input(Entrada_de_Dados), .Output(out5));
  Registrador _6 (.CLK(CLK6), .RESET(Reset), .Input(Entrada_de_Dados), .Output(out6));
  Registrador _7 (.CLK(CLK7), .RESET(Reset), .Input(Entrada_de_Dados), .Output(out7));
  Registrador _8 (.CLK(CLK8), .RESET(Reset), .Input(Entrada_de_Dados), .Output(out8));
  Registrador _9 (.CLK(CLK9), .RESET(Reset), .Input(Entrada_de_Dados), .Output(out9));
  Registrador _10 (.CLK(CLK10), .RESET(Reset), .Input(Entrada_de_Dados), .Output(out10));
  Registrador _11 (.CLK(CLK11), .RESET(Reset), .Input(Entrada_de_Dados), .Output(out11));
  Registrador _12 (.CLK(CLK12), .RESET(Reset), .Input(Entrada_de_Dados), .Output(out12));
  Registrador _13 (.CLK(CLK13), .RESET(Reset), .Input(Entrada_de_Dados), .Output(out13));
  Registrador _14 (.CLK(CLK14), .RESET(Reset), .Input(Entrada_de_Dados), .Output(out14));
  Registrador _15 (.CLK(CLK15), .RESET(Reset), .Input(Entrada_de_Dados), .Output(out15));
  Registrador _16 (.CLK(CLK16), .RESET(Reset), .Input(Entrada_de_Dados), .Output(out16));
  Registrador _17 (.CLK(CLK17), .RESET(Reset), .Input(Entrada_de_Dados), .Output(out17));
  Registrador _18 (.CLK(CLK18), .RESET(Reset), .Input(Entrada_de_Dados), .Output(out18));
  Registrador _19 (.CLK(CLK19), .RESET(Reset), .Input(Entrada_de_Dados), .Output(out19));
  Registrador _20 (.CLK(CLK20), .RESET(Reset), .Input(Entrada_de_Dados), .Output(out20));
  Registrador _21 (.CLK(CLK21), .RESET(Reset), .Input(Entrada_de_Dados), .Output(out21));
  Registrador _22 (.CLK(CLK22), .RESET(Reset), .Input(Entrada_de_Dados), .Output(out22));
  Registrador _23 (.CLK(CLK23), .RESET(Reset), .Input(Entrada_de_Dados), .Output(out23));
  Registrador _24 (.CLK(CLK24), .RESET(Reset), .Input(Entrada_de_Dados), .Output(out24));
  Registrador _25 (.CLK(CLK25), .RESET(Reset), .Input(Entrada_de_Dados), .Output(out25));
  Registrador _26 (.CLK(CLK26), .RESET(Reset), .Input(Entrada_de_Dados), .Output(out26));
  Registrador _27 (.CLK(CLK27), .RESET(Reset), .Input(Entrada_de_Dados), .Output(out27));
  Registrador _28 (.CLK(CLK28), .RESET(Reset), .Input(Entrada_de_Dados), .Output(out28));
  Registrador _29 (.CLK(CLK29), .RESET(Reset), .Input(Entrada_de_Dados), .Output(out29));
  Registrador _30 (.CLK(CLK30), .RESET(Reset), .Input(Entrada_de_Dados), .Output(out30));
  Registrador _31 (.CLK(CLK31), .RESET(Reset), .Input(Entrada_de_Dados), .Output(out31));
  Multiplexer #(.select(5), .width(32), .enable("false")) multiplexer_1 (
    .in0({32{1'b0}}), .in1(out1), .in2(out2), .in3(out3), .in4(out4), .in5(out5), .in6(out6), .in7(out7),
    .in8(out8), .in9(out9), .in10(out10), .in11(out11), .in12(out12), .in13(out13), .in14(out14),
    .in15(out15), .in16(out16), .in17(out17), .in18(out18), .in19(out19), .in20(out20), .in21(out21),
    .in22(out22), .in23(out23), .in24(out24), .in25(out25), .in26(out26), .in27(out27), .in28(out28),
    .in29(out29), .in30(out30), .in31(out31), .out(Dados_Registrador_B), .sel(Seletor_Registrador_B));
  Multiplexer #(.select(5), .width(32), .enable("false")) multiplexer_2 (
    .in0({32{1'b0}}), .in1(out1), .in2(out2), .in3(out3), .in4(out4), .in5(out5), .in6(out6), .in7(out7),
    .in8(out8), .in9(out9), .in10(out10), .in11(out11), .in12(out12), .in13(out13), .in14(out14),
    .in15(out15), .in16(out16), .in17(out17), .in18(out18), .in19(out19), .in20(out20), .in21(out21),
    .in22(out22), .in23(out23), .in24(out24), .in25(out25), .in26(out26), .in27(out27), .in28(out28),
    .in29(out29), .in30(out30), .in31(out31), .out(Dados_Registrador_A), .sel(Seletor_Registrador_A));
endmodule

module Via_De_Dados (
  input  CLK,
  input  RESET,
  input  [31:0] \Instrução ,
  output [1:0] Addr
);

  wire not_1_out, ula_32_1_overflow_soma;
  wire [31:0] banco_de_registradores_1_dados_registrador_a, banco_de_registradores_1_dados_registrador_b,
       multiplexer_1_out, n11para32_1_out_32, ula_32_1_u;

  not not_1 (not_1_out, CLK);
  PC pc_1 (.CLK(not_1_out), .RESET(RESET), .Addr(Addr));
  Banco_de_Registradores banco_de_registradores_1 (
    .CLK(CLK), .Dados_Registrador_A(banco_de_registradores_1_dados_registrador_a),
    .Dados_Registrador_B(banco_de_registradores_1_dados_registrador_b), .Entrada_de_Dados(ula_32_1_u),
    .Reset(RESET), .in_5(\Instrução [26:22]), .Seletor_Registrador_B(\Instrução [16:12]),
    .Seletor_Registrador_A(\Instrução [21:17]));
  _11para32 u_11para32_1 (.in_11(\Instrução [11:1]), .out_32(n11para32_1_out_32));
  Multiplexer #(.width(32), .enable("false")) multiplexer_1 (
    .in0(banco_de_registradores_1_dados_registrador_b), .in1(n11para32_1_out_32), .out(multiplexer_1_out),
    .sel(\Instrução [0]));
  LED led_1 (.in(ula_32_1_overflow_soma));
  ULA_32 ula_32_1 (
    .A(banco_de_registradores_1_dados_registrador_a), .B(multiplexer_1_out), .U(ula_32_1_u),
    .\Operação (\Instrução [31:27]), .OVERFLOW_SOMA(ula_32_1_overflow_soma));
  MENU menu_1 ();

  // Other names for the same wires on the sheet: i = \Instrução [0]; EXTERNO__11bits[10:0] = \Instrução [11:1];
  //   SEL_REG_B[4:0] = \Instrução [16:12]; SEL_REG_A[4:0] = \Instrução [21:17]; SEL_CLK[4:0] = \Instrução [26:22];
  //   SEL_OPERCODE[4:0] = \Instrução [31:27]

  // Notes on the sheet:
  //   soma
  //   opcode + regW + regA + regB + Ext             + i
  //   01110 + 00001 + 00000+ 00000  +00000011111 + 1 
  //   01110 + 00010 + 00000 + 00000 + 01111100000 + 1
  //   01110 + 00011 + 00001 + 00010 + 00000000000 + 0
  //   01111 + 00100 + 00000 + 00000 + 00000000000 + 1
  //   01111 + 00101 + 00000 + 00000 + 00000000001 + 1
  //   01111 + 00110 + 00100 + 00101 + 00000000000 + 0
  //   01111 + 00111 + 00110 + 00101 + 00000000000 + 0
  //   0111 0000 0100 0000 0000 0000 0011 1111
  //   0111 0000 1000 0000 0000 0111 1100 0001
  //   0111 0000 1100 0010 0010 0000 0000 0000
  //   0111 1001 0000 0000 0000 0000 0000 0001
  //   0111 1001 0100 0000 0000 0000 0000 0011
  //   0111 1001 1000 1000 0101 0000 0000 0000
  //   0111 1001 1100 1100 0101 0000 0000 0000
  //   7040003F
  //   708007C1
  //   70C22000
  //   79000001
  //   79400003
  //   79885000
  //   79CC5000
  //   soma
  //   subtração
endmodule

module INJETAR_DADOS (
  input  [31:0] in_1,
  input  [4:0] SEL_CLK,
  input  [4:0] SEL_REG_A,
  input  [4:0] SEL_REG_B,
  output [31:0] out_5,
  output [31:0] out_6
);

  wire CLK_out, R_out;

  Button CLK (.out(CLK_out));
  Button R (.out(R_out));
  Banco_de_Registradores banco_de_registradores_1 (
    .CLK(CLK_out), .Dados_Registrador_A(out_5), .Dados_Registrador_B(out_6), .Entrada_de_Dados(in_1),
    .Reset(R_out), .in_5(SEL_CLK), .Seletor_Registrador_B(SEL_REG_B), .Seletor_Registrador_A(SEL_REG_A));
endmodule

module _11para32 (
  input  [10:0] in_11,
  output [31:0] out_32
);


  assign out_32 = {{22{in_11[10]}}, in_11[9:0]};
endmodule

module PC (
  input  CLK,
  input  RESET,
  output [1:0] Addr
);

  wire [1:0] adder_1_out;

  Adder #(.width(2)) adder_1 (.a(Addr), .b(2'b01), .out(adder_1_out));  // open: cin, cout
  Register #(.width(2)) register_1 (.D(adder_1_out), .Q(Addr), .clk(CLK), .clr(RESET));  // open: en
endmodule

module computador (
);

  wire C_out, reset;
  wire [1:0] addr;
  wire [31:0] ram_1_data;

  Button C (.out(C_out));
  Button R (.out(reset));
  RAM #(.addrWidth(2), .dataWidth(32)) ram_1 (.addr(addr), .data(ram_1_data), .clr(reset));  // open: sel, clk, ld
  Via_De_Dados via_de_dados_1 (.CLK(C_out), .RESET(reset), .Addr(addr), .\Instrução (ram_1_data));

  // Notes on the sheet:
  //   soma
  //   7040003F
  //   708007C1
  //   70C22000
  //   subtração
  //   79000001
  //   79400003
  //   79885000
  //   79CC5000
endmodule
