// Logisim project ARITMETICA_32_BITS_SOMA_SUBTRAI_CORRIGIDO.circ as structural Verilog: 3 circuits, main circuit main
module main (
  input  [31:0] in_1,
  input  [31:0] in_2,
  output out_3,
  output [31:0] out_4,
  output out_5,
  output [31:0] out_6
);

  SOMADOR_32BITS somador_32bits_1 (
    .OVERFLOW(out_3), .S31(out_4[31]), .S30(out_4[30]), .A31(in_1[31]), .A30(in_1[30]), .S29(out_4[29]),
    .A29(in_1[29]), .A28(in_1[28]), .A27(in_1[27]), .S28(out_4[28]), .A26(in_1[26]), .A25(in_1[25]),
    .A24(in_1[24]), .A23(in_1[23]), .S27(out_4[27]), .A22(in_1[22]), .A21(in_1[21]), .A20(in_1[20]),
    .S26(out_4[26]), .A19(in_1[19]), .A18(in_1[18]), .A17(in_1[17]), .A16(in_1[16]), .S25(out_4[25]),
    .A15(in_1[15]), .A14(in_1[14]), .A13(in_1[13]), .S24(out_4[24]), .A12(in_1[12]), .A11(in_1[11]),
    .A10(in_1[10]), .A9(in_1[9]), .S23(out_4[23]), .A8(in_1[8]), .A7(in_1[7]), .A6(in_1[6]), .S22(out_4[22]),
    .A5(in_1[5]), .A4(in_1[4]), .A3(in_1[3]), .A2(in_1[2]), .S21(out_4[21]), .A1(in_1[1]), .A0(in_1[0]),
    .S20(out_4[20]), .S19(out_4[19]), .S18(out_4[18]), .B31(in_2[31]), .B30(in_2[30]), .B29(in_2[29]),
    .S17(out_4[17]), .B28(in_2[28]), .B27(in_2[27]), .B26(in_2[26]), .B25(in_2[25]), .S16(out_4[16]),
    .B24(in_2[24]), .B23(in_2[23]), .B22(in_2[22]), .S15(out_4[15]), .B21(in_2[21]), .B20(in_2[20]),
    .B19(in_2[19]), .B18(in_2[18]), .S14(out_4[14]), .B17(in_2[17]), .B16(in_2[16]), .B15(in_2[15]),
    .S13(out_4[13]), .B14(in_2[14]), .B13(in_2[13]), .B12(in_2[12]), .B11(in_2[11]), .S12(out_4[12]),
    .B10(in_2[10]), .B9(in_2[9]), .B8(in_2[8]), .S11(out_4[11]), .B7(in_2[7]), .B6(in_2[6]), .B5(in_2[5]),
    .B4(in_2[4]), .S10(out_4[10]), .B3(in_2[3]), .B2(in_2[2]), .B1(in_2[1]), .S9(out_4[9]), .B0(in_2[0]),
    .S8(out_4[8]), .S7(out_4[7]), .S6(out_4[6]), .S5(out_4[5]), .S4(out_4[4]), .S3(out_4[3]), .S2(out_4[2]),
    .S1(out_4[1]), .S0(out_4[0]));
  SUBTRATOR_32BITS subtrator_32bits_1 (
    .OVERFLOW(out_5), .S31(out_6[31]), .S30(out_6[30]), .A31(in_1[31]), .A30(in_1[30]), .S29(out_6[29]),
    .A29(in_1[29]), .A28(in_1[28]), .A27(in_1[27]), .S28(out_6[28]), .A26(in_1[26]), .A25(in_1[25]),
    .A24(in_1[24]), .A23(in_1[23]), .S27(out_6[27]), .A22(in_1[22]), .A21(in_1[21]), .A20(in_1[20]),
    .S26(out_6[26]), .A19(in_1[19]), .A18(in_1[18]), .A17(in_1[17]), .A16(in_1[16]), .S25(out_6[25]),
    .A15(in_1[15]), .A14(in_1[14]), .A13(in_1[13]), .S24(out_6[24]), .A12(in_1[12]), .A11(in_1[11]),
    .A10(in_1[10]), .A9(in_1[9]), .S23(out_6[23]), .A8(in_1[8]), .A7(in_1[7]), .A6(in_1[6]), .S22(out_6[22]),
    .A5(in_1[5]), .A4(in_1[4]), .A3(in_1[3]), .A2(in_1[2]), .S21(out_6[21]), .A1(in_1[1]), .A0(in_1[0]),
    .S20(out_6[20]), .S19(out_6[19]), .S18(out_6[18]), .B31(in_2[31]), .B30(in_2[30]), .B29(in_2[29]),
    .S17(out_6[17]), .B28(in_2[28]), .B27(in_2[27]), .B26(in_2[26]), .B25(in_2[25]), .S16(out_6[16]),
    .B24(in_2[24]), .B23(in_2[23]), .B22(in_2[22]), .S15(out_6[15]), .B21(in_2[21]), .B20(in_2[20]),
    .B19(in_2[19]), .B18(in_2[18]), .S14(out_6[14]), .B17(in_2[17]), .B16(in_2[16]), .B15(in_2[15]),
    .S13(out_6[13]), .B14(in_2[14]), .B13(in_2[13]), .B12(in_2[12]), .B11(in_2[11]), .S12(out_6[12]),
    .B10(in_2[10]), .B9(in_2[9]), .B8(in_2[8]), .S11(out_6[11]), .B7(in_2[7]), .B6(in_2[6]), .B5(in_2[5]),
    .B4(in_2[4]), .S10(out_6[10]), .B3(in_2[3]), .B2(in_2[2]), .B1(in_2[1]), .S9(out_6[9]), .B0(in_2[0]),
    .S8(out_6[8]), .S7(out_6[7]), .S6(out_6[6]), .S5(out_6[5]), .S4(out_6[4]), .S3(out_6[3]), .S2(out_6[2]),
    .S1(out_6[1]), .S0(out_6[0]));
endmodule

// GSOMA32
module SOMADOR_32BITS (
  input  A31,
  input  A30,
  input  A29,
  input  A28,
  input  A27,
  input  A26,
  input  A25,
  input  A24,
  input  A23,
  input  A22,
  input  A21,
  input  A20,
  input  A19,
  input  A18,
  input  A17,
  input  A16,
  input  A15,
  input  A14,
  input  A13,
  input  A12,
  input  A11,
  input  A10,
  input  A9,
  input  A8,
  input  A7,
  input  A6,
  input  A5,
  input  A4,
  input  A3,
  input  A2,
  input  A1,
  input  A0,
  input  B31,
  input  B30,
  input  B29,
  input  B28,
  input  B27,
  input  B26,
  input  B25,
  input  B24,
  input  B23,
  input  B22,
  input  B21,
  input  B20,
  input  B19,
  input  B18,
  input  B17,
  input  B16,
  input  B15,
  input  B14,
  input  B13,
  input  B12,
  input  B11,
  input  B10,
  input  B9,
  input  B8,
  input  B7,
  input  B6,
  input  B5,
  input  B4,
  input  B3,
  input  B2,
  input  B1,
  input  B0,
  output OVERFLOW,
  output S31,
  output S30,
  output S29,
  output S28,
  output S27,
  output S26,
  output S25,
  output S24,
  output S23,
  output S22,
  output S21,
  output S20,
  output S19,
  output S18,
  output S17,
  output S16,
  output S15,
  output S14,
  output S13,
  output S12,
  output S11,
  output S10,
  output S9,
  output S8,
  output S7,
  output S6,
  output S5,
  output S4,
  output S3,
  output S2,
  output S1,
  output S0
);

  wire somador_2_vai_1, somador_3_vai_1, somador_4_vai_1, somador_5_vai_1, somador_6_vai_1, somador_7_vai_1,
       somador_8_vai_1, somador_9_vai_1, somador_10_vai_1, somador_11_vai_1, somador_12_vai_1,
       somador_13_vai_1, somador_14_vai_1, somador_15_vai_1, somador_16_vai_1, somador_17_vai_1,
       somador_18_vai_1, somador_19_vai_1, somador_20_vai_1, somador_21_vai_1, somador_22_vai_1,
       somador_23_vai_1, somador_24_vai_1, somador_25_vai_1, somador_26_vai_1, somador_27_vai_1,
       somador_28_vai_1, somador_29_vai_1, somador_30_vai_1, somador_31_vai_1, somador_32_vai_1;

  SOMADOR somador_1 (.VEM_1(somador_2_vai_1), .A(A31), .B(B31), .SOMA(S31), .VAI_1(OVERFLOW));
  SOMADOR somador_2 (.VEM_1(somador_3_vai_1), .A(A30), .B(B30), .SOMA(S30), .VAI_1(somador_2_vai_1));
  SOMADOR somador_3 (.VEM_1(somador_4_vai_1), .A(A29), .B(B29), .SOMA(S29), .VAI_1(somador_3_vai_1));
  SOMADOR somador_4 (.VEM_1(somador_5_vai_1), .A(A28), .B(B28), .SOMA(S28), .VAI_1(somador_4_vai_1));
  SOMADOR somador_5 (.VEM_1(somador_6_vai_1), .A(A27), .B(B27), .SOMA(S27), .VAI_1(somador_5_vai_1));
  SOMADOR somador_6 (.VEM_1(somador_7_vai_1), .A(A26), .B(B26), .SOMA(S26), .VAI_1(somador_6_vai_1));
  SOMADOR somador_7 (.VEM_1(somador_8_vai_1), .A(A25), .B(B25), .SOMA(S25), .VAI_1(somador_7_vai_1));
  SOMADOR somador_8 (.VEM_1(somador_9_vai_1), .A(A24), .B(B24), .SOMA(S24), .VAI_1(somador_8_vai_1));
  SOMADOR somador_9 (.VEM_1(somador_10_vai_1), .A(A23), .B(B23), .SOMA(S23), .VAI_1(somador_9_vai_1));
  SOMADOR somador_10 (.VEM_1(somador_11_vai_1), .A(A22), .B(B22), .SOMA(S22), .VAI_1(somador_10_vai_1));
  SOMADOR somador_11 (.VEM_1(somador_12_vai_1), .A(A21), .B(B21), .SOMA(S21), .VAI_1(somador_11_vai_1));
  SOMADOR somador_12 (.VEM_1(somador_13_vai_1), .A(A20), .B(B20), .SOMA(S20), .VAI_1(somador_12_vai_1));
  SOMADOR somador_13 (.VEM_1(somador_14_vai_1), .A(A19), .B(B19), .SOMA(S19), .VAI_1(somador_13_vai_1));
  SOMADOR somador_14 (.VEM_1(somador_16_vai_1), .A(A18), .B(B18), .SOMA(S18), .VAI_1(somador_14_vai_1));
  SOMADOR somador_15 (.VEM_1(somador_17_vai_1), .A(A16), .B(B16), .SOMA(S16), .VAI_1(somador_15_vai_1));
  SOMADOR somador_16 (.VEM_1(somador_15_vai_1), .A(A17), .B(B17), .SOMA(S17), .VAI_1(somador_16_vai_1));
  SOMADOR somador_17 (.VEM_1(somador_18_vai_1), .A(A15), .B(B15), .SOMA(S15), .VAI_1(somador_17_vai_1));
  SOMADOR somador_18 (.VEM_1(somador_19_vai_1), .A(A14), .B(B14), .SOMA(S14), .VAI_1(somador_18_vai_1));
  SOMADOR somador_19 (.VEM_1(somador_20_vai_1), .A(A13), .B(B13), .SOMA(S13), .VAI_1(somador_19_vai_1));
  SOMADOR somador_20 (.VEM_1(somador_21_vai_1), .A(A12), .B(B12), .SOMA(S12), .VAI_1(somador_20_vai_1));
  SOMADOR somador_21 (.VEM_1(somador_22_vai_1), .A(A11), .B(B11), .SOMA(S11), .VAI_1(somador_21_vai_1));
  SOMADOR somador_22 (.VEM_1(somador_23_vai_1), .A(A10), .B(B10), .SOMA(S10), .VAI_1(somador_22_vai_1));
  SOMADOR somador_23 (.VEM_1(somador_24_vai_1), .A(A9), .B(B9), .SOMA(S9), .VAI_1(somador_23_vai_1));
  SOMADOR somador_24 (.VEM_1(somador_25_vai_1), .A(A8), .B(B8), .SOMA(S8), .VAI_1(somador_24_vai_1));
  SOMADOR somador_25 (.VEM_1(somador_26_vai_1), .A(A7), .B(B7), .SOMA(S7), .VAI_1(somador_25_vai_1));
  SOMADOR somador_26 (.VEM_1(somador_27_vai_1), .A(A6), .B(B6), .SOMA(S6), .VAI_1(somador_26_vai_1));
  SOMADOR somador_27 (.VEM_1(somador_28_vai_1), .A(A5), .B(B5), .SOMA(S5), .VAI_1(somador_27_vai_1));
  SOMADOR somador_28 (.VEM_1(somador_29_vai_1), .A(A4), .B(B4), .SOMA(S4), .VAI_1(somador_28_vai_1));
  SOMADOR somador_29 (.VEM_1(somador_30_vai_1), .A(A3), .B(B3), .SOMA(S3), .VAI_1(somador_29_vai_1));
  SOMADOR somador_30 (.VEM_1(somador_31_vai_1), .A(A2), .B(B2), .SOMA(S2), .VAI_1(somador_30_vai_1));
  SOMADOR somador_31 (.VEM_1(somador_32_vai_1), .A(A1), .B(B1), .SOMA(S1), .VAI_1(somador_31_vai_1));
  SOMADOR somador_32 (.VEM_1(1'b0), .A(A0), .B(B0), .SOMA(S0), .VAI_1(somador_32_vai_1));
endmodule

// GSUBTRAI32
module SUBTRATOR_32BITS (
  input  A31,
  input  A30,
  input  A29,
  input  A28,
  input  A27,
  input  A26,
  input  A25,
  input  A24,
  input  A23,
  input  A22,
  input  A21,
  input  A20,
  input  A19,
  input  A18,
  input  A17,
  input  A16,
  input  A15,
  input  A14,
  input  A13,
  input  A12,
  input  A11,
  input  A10,
  input  A9,
  input  A8,
  input  A7,
  input  A6,
  input  A5,
  input  A4,
  input  A3,
  input  A2,
  input  A1,
  input  A0,
  input  B31,
  input  B30,
  input  B29,
  input  B28,
  input  B27,
  input  B26,
  input  B25,
  input  B24,
  input  B23,
  input  B22,
  input  B21,
  input  B20,
  input  B19,
  input  B18,
  input  B17,
  input  B16,
  input  B15,
  input  B14,
  input  B13,
  input  B12,
  input  B11,
  input  B10,
  input  B9,
  input  B8,
  input  B7,
  input  B6,
  input  B5,
  input  B4,
  input  B3,
  input  B2,
  input  B1,
  input  B0,
  output OVERFLOW,
  output S31,
  output S30,
  output S29,
  output S28,
  output S27,
  output S26,
  output S25,
  output S24,
  output S23,
  output S22,
  output S21,
  output S20,
  output S19,
  output S18,
  output S17,
  output S16,
  output S15,
  output S14,
  output S13,
  output S12,
  output S11,
  output S10,
  output S9,
  output S8,
  output S7,
  output S6,
  output S5,
  output S4,
  output S3,
  output S2,
  output S1,
  output S0
);

  wire subtrator_2_vai_1, subtrator_3_vai_1, subtrator_4_vai_1, subtrator_5_vai_1, subtrator_6_vai_1,
       subtrator_7_vai_1, subtrator_8_vai_1, subtrator_9_vai_1, subtrator_10_vai_1, subtrator_11_vai_1,
       subtrator_12_vai_1, subtrator_13_vai_1, subtrator_14_vai_1, subtrator_15_vai_1, subtrator_16_vai_1,
       subtrator_17_vai_1, subtrator_18_vai_1, subtrator_19_vai_1, subtrator_20_vai_1, subtrator_21_vai_1,
       subtrator_22_vai_1, subtrator_23_vai_1, subtrator_24_vai_1, subtrator_25_vai_1, subtrator_26_vai_1,
       subtrator_27_vai_1, subtrator_28_vai_1, subtrator_29_vai_1, subtrator_30_vai_1, subtrator_31_vai_1,
       subtrator_32_vai_1;

  SUBTRATOR subtrator_1 (.VEM_1(subtrator_2_vai_1), .A(A31), .B(B31), .\SUBTRAÇÃO (S31), .VAI_1(OVERFLOW));
  SUBTRATOR subtrator_2 (.VEM_1(subtrator_3_vai_1), .A(A30), .B(B30), .\SUBTRAÇÃO (S30), .VAI_1(subtrator_2_vai_1));
  SUBTRATOR subtrator_3 (.VEM_1(subtrator_4_vai_1), .A(A29), .B(B29), .\SUBTRAÇÃO (S29), .VAI_1(subtrator_3_vai_1));
  SUBTRATOR subtrator_4 (.VEM_1(subtrator_5_vai_1), .A(A28), .B(B28), .\SUBTRAÇÃO (S28), .VAI_1(subtrator_4_vai_1));
  SUBTRATOR subtrator_5 (.VEM_1(subtrator_6_vai_1), .A(A27), .B(B27), .\SUBTRAÇÃO (S27), .VAI_1(subtrator_5_vai_1));
  SUBTRATOR subtrator_6 (.VEM_1(subtrator_7_vai_1), .A(A26), .B(B26), .\SUBTRAÇÃO (S26), .VAI_1(subtrator_6_vai_1));
  SUBTRATOR subtrator_7 (.VEM_1(subtrator_8_vai_1), .A(A25), .B(B25), .\SUBTRAÇÃO (S25), .VAI_1(subtrator_7_vai_1));
  SUBTRATOR subtrator_8 (.VEM_1(subtrator_9_vai_1), .A(A24), .B(B24), .\SUBTRAÇÃO (S24), .VAI_1(subtrator_8_vai_1));
  SUBTRATOR subtrator_9 (.VEM_1(subtrator_10_vai_1), .A(A23), .B(B23), .\SUBTRAÇÃO (S23), .VAI_1(subtrator_9_vai_1));
  SUBTRATOR subtrator_10 (.VEM_1(subtrator_11_vai_1), .A(A22), .B(B22), .\SUBTRAÇÃO (S22), .VAI_1(subtrator_10_vai_1));
  SUBTRATOR subtrator_11 (.VEM_1(subtrator_12_vai_1), .A(A21), .B(B21), .\SUBTRAÇÃO (S21), .VAI_1(subtrator_11_vai_1));
  SUBTRATOR subtrator_12 (.VEM_1(subtrator_13_vai_1), .A(A20), .B(B20), .\SUBTRAÇÃO (S20), .VAI_1(subtrator_12_vai_1));
  SUBTRATOR subtrator_13 (.VEM_1(subtrator_14_vai_1), .A(A19), .B(B19), .\SUBTRAÇÃO (S19), .VAI_1(subtrator_13_vai_1));
  SUBTRATOR subtrator_14 (.VEM_1(subtrator_15_vai_1), .A(A18), .B(B18), .\SUBTRAÇÃO (S18), .VAI_1(subtrator_14_vai_1));
  SUBTRATOR subtrator_15 (.VEM_1(subtrator_17_vai_1), .A(A17), .B(B17), .\SUBTRAÇÃO (S17), .VAI_1(subtrator_15_vai_1));
  SUBTRATOR subtrator_16 (.VEM_1(subtrator_18_vai_1), .A(A15), .B(B15), .\SUBTRAÇÃO (S15), .VAI_1(subtrator_16_vai_1));
  SUBTRATOR subtrator_17 (.VEM_1(subtrator_16_vai_1), .A(A16), .B(B16), .\SUBTRAÇÃO (S16), .VAI_1(subtrator_17_vai_1));
  SUBTRATOR subtrator_18 (.VEM_1(subtrator_19_vai_1), .A(A14), .B(B14), .\SUBTRAÇÃO (S14), .VAI_1(subtrator_18_vai_1));
  SUBTRATOR subtrator_19 (.VEM_1(subtrator_20_vai_1), .A(A13), .B(B13), .\SUBTRAÇÃO (S13), .VAI_1(subtrator_19_vai_1));
  SUBTRATOR subtrator_20 (.VEM_1(subtrator_21_vai_1), .A(A12), .B(B12), .\SUBTRAÇÃO (S12), .VAI_1(subtrator_20_vai_1));
  SUBTRATOR subtrator_21 (.VEM_1(subtrator_22_vai_1), .A(A11), .B(B11), .\SUBTRAÇÃO (S11), .VAI_1(subtrator_21_vai_1));
  SUBTRATOR subtrator_22 (.VEM_1(subtrator_23_vai_1), .A(A10), .B(B10), .\SUBTRAÇÃO (S10), .VAI_1(subtrator_22_vai_1));
  SUBTRATOR subtrator_23 (.VEM_1(subtrator_24_vai_1), .A(A9), .B(B9), .\SUBTRAÇÃO (S9), .VAI_1(subtrator_23_vai_1));
  SUBTRATOR subtrator_24 (.VEM_1(subtrator_25_vai_1), .A(A8), .B(B8), .\SUBTRAÇÃO (S8), .VAI_1(subtrator_24_vai_1));
  SUBTRATOR subtrator_25 (.VEM_1(subtrator_26_vai_1), .A(A7), .B(B7), .\SUBTRAÇÃO (S7), .VAI_1(subtrator_25_vai_1));
  SUBTRATOR subtrator_26 (.VEM_1(subtrator_27_vai_1), .A(A6), .B(B6), .\SUBTRAÇÃO (S6), .VAI_1(subtrator_26_vai_1));
  SUBTRATOR subtrator_27 (.VEM_1(subtrator_28_vai_1), .A(A5), .B(B5), .\SUBTRAÇÃO (S5), .VAI_1(subtrator_27_vai_1));
  SUBTRATOR subtrator_28 (.VEM_1(subtrator_29_vai_1), .A(A4), .B(B4), .\SUBTRAÇÃO (S4), .VAI_1(subtrator_28_vai_1));
  SUBTRATOR subtrator_29 (.VEM_1(subtrator_30_vai_1), .A(A3), .B(B3), .\SUBTRAÇÃO (S3), .VAI_1(subtrator_29_vai_1));
  SUBTRATOR subtrator_30 (.VEM_1(subtrator_31_vai_1), .A(A2), .B(B2), .\SUBTRAÇÃO (S2), .VAI_1(subtrator_30_vai_1));
  SUBTRATOR subtrator_31 (.VEM_1(subtrator_32_vai_1), .A(A1), .B(B1), .\SUBTRAÇÃO (S1), .VAI_1(subtrator_31_vai_1));
  SUBTRATOR subtrator_32 (.VEM_1(1'b0), .A(A0), .B(B0), .\SUBTRAÇÃO (S0), .VAI_1(subtrator_32_vai_1));
endmodule
