// Logisim project DEMUX.circ as structural Verilog
module DEMUX_2 (
  input  \Informação_Multiplexada ,
  input  Seletor_0,
  output A,
  output B
);

  and and_1 (A, ~Seletor_0, \Informação_Multiplexada );  // AND_Gate
  and and_2 (B, \Informação_Multiplexada , Seletor_0);
endmodule

module DEMUX_4 (
  input  \Informação_Multiplexada ,
  input  Seletor_1,
  input  Seletor_0,
  output A,
  output B,
  output C,
  output D
);

  wire demux_2_1_a, demux_2_1_b;

  DEMUX_2 demux_2_1 (
    .\Informação_Multiplexada (\Informação_Multiplexada ), .Seletor_0(Seletor_1), .A(demux_2_1_a),
    .B(demux_2_1_b));
  DEMUX_2 demux_2_2 (.\Informação_Multiplexada (demux_2_1_a), .Seletor_0(Seletor_0), .A(A), .B(B));
  DEMUX_2 demux_2_3 (.\Informação_Multiplexada (demux_2_1_b), .Seletor_0(Seletor_0), .A(C), .B(D));
endmodule

module DEMUX_8 (
  input  \Informação_Multiplexada ,
  input  S2,
  input  S1,
  input  S0,
  output A,
  output B,
  output C,
  output D,
  output E,
  output F,
  output G,
  output H
);

  wire demux_2_1_a, demux_2_1_b;

  DEMUX_2 demux_2_1 (
    .\Informação_Multiplexada (\Informação_Multiplexada ), .Seletor_0(S2), .A(demux_2_1_a), .B(demux_2_1_b));
  DEMUX_4 demux_4_1 (
    .\Informação_Multiplexada (demux_2_1_a), .Seletor_1(S1), .Seletor_0(S0), .A(A), .B(B), .C(C), .D(D));
  DEMUX_4 demux_4_2 (
    .\Informação_Multiplexada (demux_2_1_b), .Seletor_1(S1), .Seletor_0(S0), .A(E), .B(F), .C(G), .D(H));
endmodule

module DEMUX_16 (
  input  \Informação_Multiplexada ,
  input  S3,
  input  S2,
  input  S1,
  input  S0,
  output A,
  output B,
  output C,
  output D,
  output E,
  output F,
  output G,
  output H,
  output I,
  output J,
  output K,
  output L,
  output N,
  output M,
  output O,
  output P
);

  wire demux_2_1_a, demux_2_1_b;

  DEMUX_2 demux_2_1 (
    .\Informação_Multiplexada (\Informação_Multiplexada ), .Seletor_0(S3), .A(demux_2_1_a), .B(demux_2_1_b));
  DEMUX_8 demux_8_1 (
    .\Informação_Multiplexada (demux_2_1_a), .S2(S2), .S1(S1), .S0(S0), .A(A), .B(B), .C(C), .D(D), .E(E),
    .F(F), .G(G), .H(H));
  DEMUX_8 demux_8_2 (
    .\Informação_Multiplexada (demux_2_1_b), .S2(S2), .S1(S1), .S0(S0), .A(I), .B(J), .C(K), .D(L), .E(N),
    .F(M), .G(O), .H(P));

  // Other names for the same wires on the sheet: SEL123[2:0] = {S2, S1, S0}
endmodule

module DEMUX_32 (
  input  \Informação_Multiplexada ,
  input  S4,
  input  S3,
  input  S2,
  input  S1,
  input  S0,
  output A,
  output B,
  output C,
  output D,
  output E,
  output F,
  output G,
  output H,
  output I,
  output J,
  output K,
  output L,
  output N,
  output M,
  output O,
  output P,
  output Q,
  output R,
  output S,
  output T,
  output U,
  output V,
  output W,
  output X,
  output Y,
  output Z,
  output Z1,
  output Z2,
  output Z3,
  output Z4,
  output Z5,
  output Z6
);

  wire demux_2_1_a, demux_2_1_b;

  DEMUX_2 demux_2_1 (
    .\Informação_Multiplexada (\Informação_Multiplexada ), .Seletor_0(S4), .A(demux_2_1_a), .B(demux_2_1_b));
  DEMUX_16 demux_16_1 (
    .\Informação_Multiplexada (demux_2_1_a), .S3(S3), .S2(S2), .S1(S1), .S0(S0), .A(A), .B(B), .C(C), .D(D),
    .E(E), .F(F), .G(G), .H(H), .I(I), .J(J), .K(K), .L(L), .N(N), .M(M), .O(O), .P(P));
  DEMUX_16 demux_16_2 (
    .\Informação_Multiplexada (demux_2_1_b), .S3(S3), .S2(S2), .S1(S1), .S0(S0), .A(Q), .B(R), .C(S), .D(T),
    .E(U), .F(V), .G(W), .H(X), .I(Y), .J(Z), .K(Z1), .L(Z2), .N(Z3), .M(Z4), .O(Z5), .P(Z6));

  // Other names for the same wires on the sheet: SEL1234[3:0] = {S3, S2, S1, S0}

  // Notes on the sheet:
  //   DEMUX 32 BITS
endmodule
