// Logisim project MUX.circ as structural Verilog
module MUX_2 (
  input  Entrada_0,
  input  Entrada_1,
  input  Seletor_A,
  output out_4
);

  wire and_1_out, and_2_out;

  and and_1 (and_1_out, ~Seletor_A, Entrada_0);  // AND_Gate
  and and_2 (and_2_out, Entrada_1, Seletor_A);
  or or_1 (out_4, and_1_out, and_2_out);
endmodule

module MUX_4 (
  input  Entrada_0,
  input  Entrada_1,
  input  Entrada_2,
  input  Entrada_3,
  input  Seletor_B,
  input  Seletor_A,
  output out_7
);

  wire mux_2_1_out_4, mux_2_2_out_4;

  MUX_2 mux_2_1 (.Entrada_0(Entrada_0), .Entrada_1(Entrada_1), .Seletor_A(Seletor_A), .out_4(mux_2_1_out_4));
  MUX_2 mux_2_2 (.Entrada_0(Entrada_2), .Entrada_1(Entrada_3), .Seletor_A(Seletor_A), .out_4(mux_2_2_out_4));
  MUX_2 mux_2_3 (.Entrada_0(mux_2_1_out_4), .Entrada_1(mux_2_2_out_4), .Seletor_A(Seletor_B), .out_4(out_7));
endmodule

module MUX_8 (
  input  Entrada_0,
  input  Entrada_1,
  input  Entrada_2,
  input  Entrada_3,
  input  Entrada_4,
  input  Entrada_5,
  input  Entrada_6,
  input  Entrada_7,
  input  Seletor_C,
  input  Seletor_B,
  input  Seletor_A,
  output out_12
);

  wire mux_4_1_out_7, mux_4_2_out_7;

  MUX_4 mux_4_1 (
    .Entrada_0(Entrada_0), .Entrada_1(Entrada_1), .Entrada_2(Entrada_2), .Entrada_3(Entrada_3),
    .Seletor_B(Seletor_B), .Seletor_A(Seletor_A), .out_7(mux_4_1_out_7));
  MUX_4 mux_4_2 (
    .Entrada_0(Entrada_4), .Entrada_1(Entrada_5), .Entrada_2(Entrada_6), .Entrada_3(Entrada_7),
    .Seletor_B(Seletor_B), .Seletor_A(Seletor_A), .out_7(mux_4_2_out_7));
  MUX_2 mux_2_1 (.Entrada_0(mux_4_1_out_7), .Entrada_1(mux_4_2_out_7), .Seletor_A(Seletor_C), .out_4(out_12));
endmodule

module MUX_16 (
  input  Entrada_0,
  input  Entrada_1,
  input  Entrada_2,
  input  Entrada_3,
  input  Entrada_4,
  input  Entrada_5,
  input  Entrada_6,
  input  Entrada_7,
  input  Entrada_8,
  input  Entrada_9,
  input  Entrada_10,
  input  Entrada_11,
  input  Entrada_12,
  input  Entrada_13,
  input  Entrada_14,
  input  Entrada_15,
  input  S3,
  input  S2,
  input  S1,
  input  S0,
  output out_21
);

  wire mux_8_1_out_12, mux_8_2_out_12;

  MUX_8 mux_8_1 (
    .Entrada_0(Entrada_0), .Entrada_1(Entrada_1), .Entrada_2(Entrada_2), .Entrada_3(Entrada_3),
    .Entrada_4(Entrada_4), .Entrada_5(Entrada_5), .Entrada_6(Entrada_6), .Entrada_7(Entrada_7),
    .Seletor_C(S2), .Seletor_B(S1), .Seletor_A(S0), .out_12(mux_8_1_out_12));
  MUX_8 mux_8_2 (
    .Entrada_0(Entrada_8), .Entrada_1(Entrada_9), .Entrada_2(Entrada_10), .Entrada_3(Entrada_11),
    .Entrada_4(Entrada_12), .Entrada_5(Entrada_13), .Entrada_6(Entrada_14), .Entrada_7(Entrada_15),
    .Seletor_C(S2), .Seletor_B(S1), .Seletor_A(S0), .out_12(mux_8_2_out_12));
  MUX_2 mux_2_1 (.Entrada_0(mux_8_1_out_12), .Entrada_1(mux_8_2_out_12), .Seletor_A(S3), .out_4(out_21));
endmodule

module MUX_32 (
  input  S4,
  input  S3,
  input  S2,
  input  S1,
  input  S0,
  input  Entrada_0,
  input  Entrada_1,
  input  Entrada_2,
  input  Entrada_3,
  input  Entrada_4,
  input  Entrada_5,
  input  Entrada_6,
  input  Entrada_7,
  input  Entrada_8,
  input  Entrada_9,
  input  Entrada_10,
  input  Entrada_11,
  input  Entrada_12,
  input  Entrada_13,
  input  Entrada_14,
  input  Entrada_15,
  input  Entrada_16,
  input  Entrada_17,
  input  Entrada_18,
  input  Entrada_19,
  input  Entrada_20,
  input  Entrada_21,
  input  Entrada_22,
  input  Entrada_23,
  input  Entrada_24,
  input  Entrada_25,
  input  Entrada_26,
  input  Entrada_27,
  input  Entrada_28,
  input  Entrada_29,
  input  Entrada_30,
  input  Entrada_31,
  output out_38
);

  wire mux_16_1_out_21, mux_16_2_out_21;

  MUX_16 mux_16_1 (
    .Entrada_0(Entrada_0), .Entrada_1(Entrada_1), .Entrada_2(Entrada_2), .Entrada_3(Entrada_3),
    .Entrada_4(Entrada_4), .Entrada_5(Entrada_5), .Entrada_6(Entrada_6), .Entrada_7(Entrada_7),
    .Entrada_8(Entrada_8), .Entrada_9(Entrada_9), .Entrada_10(Entrada_10), .Entrada_11(Entrada_11),
    .Entrada_12(Entrada_12), .Entrada_13(Entrada_13), .Entrada_14(Entrada_14), .Entrada_15(Entrada_15),
    .S3(S3), .S2(S2), .S1(S1), .S0(S0), .out_21(mux_16_1_out_21));
  MUX_16 mux_16_2 (
    .Entrada_0(Entrada_16), .Entrada_1(Entrada_17), .Entrada_2(Entrada_18), .Entrada_3(Entrada_19),
    .Entrada_4(Entrada_20), .Entrada_5(Entrada_21), .Entrada_6(Entrada_22), .Entrada_7(Entrada_23),
    .Entrada_8(Entrada_24), .Entrada_9(Entrada_25), .Entrada_10(Entrada_26), .Entrada_11(Entrada_27),
    .Entrada_12(Entrada_28), .Entrada_13(Entrada_29), .Entrada_14(Entrada_30), .Entrada_15(Entrada_31),
    .S3(S3), .S2(S2), .S1(S1), .S0(S0), .out_21(mux_16_2_out_21));
  MUX_2 mux_2_1 (.Entrada_0(mux_16_1_out_21), .Entrada_1(mux_16_2_out_21), .Seletor_A(S4), .out_4(out_38));

  // Other names for the same wires on the sheet: SELETOR[3:0] = {S3, S2, S1, S0}
endmodule
