// Logisim project SOMADORES.circ as structural Verilog: 4 circuits, main circuit main
module main (
);


  // Notes on the sheet:
  //   SOMA = VEM1 XOR A XOR B
  //   VAI 1 = (VEM1 AND B) OR (VEM1 AND A) OR (A AND B) 
endmodule

module somador_1bit (
  input  A,
  input  B,
  output SOMA,
  output VAI_1
);

  xor xor_1 (SOMA, B, A);
  and and_1 (VAI_1, B, A);
endmodule

module somador_4bit (
  input  [3:0] A,
  input  [3:0] B,
  output [3:0] out_3,
  output OVERFLOW
);

  wire somador_1bit_1_vai_1, somador_completo_2_bits_2_vai_1, somador_completo_2_bits_3_vai_1;

  somador_completo_2_bits somador_completo_2_bits_1 (
    .VEM_1(somador_completo_2_bits_2_vai_1), .A(A[3]), .B(B[3]), .SOMA(out_3[3]), .VAI_1(OVERFLOW));
  somador_completo_2_bits somador_completo_2_bits_2 (
    .VEM_1(somador_completo_2_bits_3_vai_1), .A(A[2]), .B(B[2]), .SOMA(out_3[2]),
    .VAI_1(somador_completo_2_bits_2_vai_1));
  somador_completo_2_bits somador_completo_2_bits_3 (
    .VEM_1(somador_1bit_1_vai_1), .A(A[1]), .B(B[1]), .SOMA(out_3[1]), .VAI_1(somador_completo_2_bits_3_vai_1));
  somador_1bit somador_1bit_1 (.A(A[0]), .B(B[0]), .SOMA(out_3[0]), .VAI_1(somador_1bit_1_vai_1));
endmodule

module somador_completo_2_bits (
  input  VEM_1,
  input  A,
  input  B,
  output SOMA,
  output VAI_1
);

  wire and_1_out, and_2_out, and_3_out;

  ExactlyOne xor_1 (.out(SOMA), .in0(B), .in1(A), .in2(VEM_1));
  and and_1 (and_1_out, VEM_1, B);
  and and_2 (and_2_out, VEM_1, A);
  and and_3 (and_3_out, A, B);
  or or_1 (VAI_1, and_1_out, and_2_out, and_3_out);
endmodule
