// Logisim project projetoCORRIGIDO.circ as structural Verilog: 9 circuits, main circuit main
module main (
);

  mux16 mux16_1 ();  // open: out_21, Canal_0, Canal_1, Canal_2, Canal_3, Canal_4, Canal_5, Canal_6, Canal_7, Canal_8, Canal_9, Canal_10, Canal_11, Canal_12, Canal_13, Canal_14, Canal_15, SEL_0, SEL_1, SEL_2, SEL_3
  mux32 mux32_1 ();  // open: out_38, P, Z6, O, Z5, N, Z4, M, Z3, L, Z2, K, Z1, J, Z, I, Y, H, X, G, W, F, V, E, U, D, T, C, S, B, R, A, Q, SEL_0, SEL_1, SEL_2, SEL_3, SEL_4
  mux16 mux16_2 ();  // open: out_21, Canal_0, Canal_1, Canal_2, Canal_3, Canal_4, Canal_5, Canal_6, Canal_7, Canal_8, Canal_9, Canal_10, Canal_11, Canal_12, Canal_13, Canal_14, Canal_15, SEL_0, SEL_1, SEL_2, SEL_3
  ULA_1_BIT ula_1_bit_1 ();  // open: VAI_1, U, VEM_1, A, B, in_4
endmodule

module mux16 (
  input  Canal_0,
  input  Canal_1,
  input  Canal_2,
  input  Canal_3,
  input  Canal_4,
  input  Canal_5,
  input  Canal_6,
  input  Canal_7,
  input  Canal_8,
  input  Canal_9,
  input  Canal_10,
  input  Canal_11,
  input  Canal_12,
  input  Canal_13,
  input  Canal_14,
  input  Canal_15,
  input  SEL_3,
  input  SEL_2,
  input  SEL_1,
  input  SEL_0,
  output out_21
);

  wire mux8_1_saida, mux8_2_saida;

  mux8 mux8_1 (
    .Canal_0(Canal_0), .Canal_1(Canal_1), .Canal_2(Canal_2), .Canal_3(Canal_3), .Canal_4(Canal_4),
    .Canal_5(Canal_5), .Canal_6(Canal_6), .Canal_7(Canal_7), .Saida(mux8_1_saida), .Sel_2(SEL_2),
    .Sel_1(SEL_1), .Sel_0(SEL_0));
  mux8 mux8_2 (
    .Canal_0(Canal_8), .Canal_1(Canal_9), .Canal_2(Canal_10), .Canal_3(Canal_11), .Canal_4(Canal_12),
    .Canal_5(Canal_13), .Canal_6(Canal_14), .Canal_7(Canal_15), .Saida(mux8_2_saida), .Sel_2(SEL_2),
    .Sel_1(SEL_1), .Sel_0(SEL_0));
  mux2 mux2_1 (.Canal_0(mux8_1_saida), .Canal_1(mux8_2_saida), .out_4(out_21), .Seletor_0(SEL_3));
endmodule

module mux8 (
  input  Canal_0,
  input  Canal_1,
  input  Canal_2,
  input  Canal_3,
  input  Canal_4,
  input  Canal_5,
  input  Canal_6,
  input  Canal_7,
  input  Sel_2,
  input  Sel_1,
  input  Sel_0,
  output Saida
);

  wire and_1_out, and_2_out, and_3_out, and_4_out, and_5_out, and_6_out, and_7_out, and_8_out;

  and and_1 (and_1_out, Canal_0, ~Sel_2, ~Sel_1, ~Sel_0);  // AND_Gate
  and and_2 (and_2_out, Canal_1, ~Sel_2, ~Sel_1, Sel_0);  // AND_Gate
  and and_3 (and_3_out, Canal_2, ~Sel_2, Sel_1, ~Sel_0);  // AND_Gate
  and and_4 (and_4_out, Canal_3, ~Sel_2, Sel_1, Sel_0);  // AND_Gate
  and and_5 (and_5_out, Canal_4, Sel_2, ~Sel_1, ~Sel_0);  // AND_Gate
  and and_6 (and_6_out, Canal_5, Sel_2, ~Sel_1, Sel_0);  // AND_Gate
  and and_7 (and_7_out, Canal_6, Sel_2, Sel_1, ~Sel_0);  // AND_Gate
  and and_8 (and_8_out, Canal_7, Sel_2, Sel_1, Sel_0);
  or or_1 (Saida, and_1_out, and_2_out, and_3_out, and_4_out, and_5_out, and_6_out, and_7_out, and_8_out);
endmodule

module mux2 (
  input  Canal_0,
  input  Canal_1,
  input  Seletor_0,
  output out_4
);

  wire and_1_out, and_2_out;

  and and_1 (and_1_out, Canal_0, ~Seletor_0);  // AND_Gate
  and and_2 (and_2_out, Canal_1, Seletor_0);
  or or_1 (out_4, and_1_out, and_2_out);
endmodule

module ULA_1_BIT (
  input  A,
  input  B,
  input  VEM_1,
  input  [4:0] in_4,
  output U,
  output VAI_1
);

  wire and_1_out, or_1_out, soma_1_soma, xor_1_out;

  and and_1 (and_1_out, A, B);
  or or_1 (or_1_out, A, B);
  xor xor_1 (xor_1_out, A, B);
  SOMA soma_1 (.SOMA(soma_1_soma), .VAI_1(VAI_1), .VEM_1(VEM_1), .B(B), .A(A));
  mux32 mux32_1 (
    .out_38(U), .D(soma_1_soma), .C(xor_1_out), .B(or_1_out), .A(and_1_out), .SEL_0(in_4[0]),
    .SEL_1(in_4[1]), .SEL_2(in_4[2]), .SEL_3(in_4[3]), .SEL_4(in_4[4]));  // open: P, Z6, O, Z5, N, Z4, M, Z3, L, Z2, K, Z1, J, Z, I, Y, H, X, G, W, F, V, E, U, T, S, R, Q
endmodule

module SOMA (
  input  VEM_1,
  input  B,
  input  A,
  output SOMA,
  output VAI_1
);

  wire and_1_out, and_2_out, and_3_out, xor_1_out;

  xor xor_1 (xor_1_out, B, A);
  and and_1 (and_1_out, A, VEM_1);
  and and_2 (and_2_out, B, VEM_1);
  and and_3 (and_3_out, A, B);
  xor xor_2 (SOMA, xor_1_out, VEM_1);
  or or_1 (VAI_1, and_1_out, and_2_out, and_3_out);
endmodule

module ULA_4BIT (
  input  [3:0] A,
  input  [3:0] B,
  input  [4:0] in_3,
  output [3:0] U,
  output OVERFLOW
);

  wire _0VAI1, _1VAI1, _2VAI1;

  ULA_1_BIT ula_1_bit_1 (.VAI_1(_0VAI1), .U(U[0]), .VEM_1(1'b0), .A(A[0]), .B(B[0]), .in_4(in_3));
  ULA_1_BIT ula_1_bit_2 (.VAI_1(_1VAI1), .U(U[1]), .VEM_1(_0VAI1), .A(A[1]), .B(B[1]), .in_4(in_3));
  ULA_1_BIT ula_1_bit_3 (.VAI_1(_2VAI1), .U(U[2]), .VEM_1(_1VAI1), .A(A[2]), .B(B[2]), .in_4(in_3));
  ULA_1_BIT ula_1_bit_4 (.VAI_1(OVERFLOW), .U(U[3]), .VEM_1(_2VAI1), .A(A[3]), .B(B[3]), .in_4(in_3));

  // Other names for the same wires on the sheet: SELETOR[4:0] = in_3

  // Notes on the sheet:
  //   000 = AND
  //   001 = OR
  //   010 = XOR
  //   011 = SOMA
endmodule

module ULA_32 (
  input  [31:0] A,
  input  [31:0] B,
  input  [4:0] in_3,
  output OVERFLOW,
  output [31:0] U
);

  wire _0VAI1, _1VAI1, _2VAI1, _3VAI1, _4VAI1, _5VAI1, _6VAI1, _7VAI1, _8VAI1, _9VAI1, _10VAI1, _11VAI1,
       _12VAI1, _13VAI1, _14VAI1, _15VAI1, _16VAI1, _17VAI1, _18VAI1, _19VAI1, _20VAI1, _21VAI1, _22VAI1,
       _23VAI1, _24VAI1, _25VAI1, _26VAI1, _27VAI1, _28VAI1, _29VAI1, _30VAI1;

  ULA_1_BIT ula_1_bit_1 (.VAI_1(_9VAI1), .U(U[9]), .VEM_1(_8VAI1), .A(A[9]), .B(B[9]), .in_4(in_3));
  ULA_1_BIT ula_1_bit_2 (.VAI_1(_19VAI1), .U(U[19]), .VEM_1(_18VAI1), .A(A[19]), .B(B[19]), .in_4(in_3));
  ULA_1_BIT ula_1_bit_3 (.VAI_1(_29VAI1), .U(U[29]), .VEM_1(_28VAI1), .A(A[29]), .B(B[19]), .in_4(in_3));
  ULA_1_BIT ula_1_bit_4 (.VAI_1(_8VAI1), .U(U[8]), .VEM_1(_7VAI1), .A(A[8]), .B(B[8]), .in_4(in_3));
  ULA_1_BIT ula_1_bit_5 (.VAI_1(_18VAI1), .U(U[18]), .VEM_1(_17VAI1), .A(A[18]), .B(B[18]), .in_4(in_3));
  ULA_1_BIT ula_1_bit_6 (.VAI_1(_28VAI1), .U(U[28]), .VEM_1(_27VAI1), .A(A[28]), .B(B[28]), .in_4(in_3));
  ULA_1_BIT ula_1_bit_7 (.VAI_1(_7VAI1), .U(U[7]), .VEM_1(_6VAI1), .A(A[7]), .B(B[7]), .in_4(in_3));
  ULA_1_BIT ula_1_bit_8 (.VAI_1(_17VAI1), .U(U[17]), .VEM_1(_16VAI1), .A(A[17]), .B(B[17]), .in_4(in_3));
  ULA_1_BIT ula_1_bit_9 (.VAI_1(_27VAI1), .U(U[27]), .VEM_1(_26VAI1), .A(A[27]), .B(B[27]), .in_4(in_3));
  ULA_1_BIT ula_1_bit_10 (.VAI_1(_6VAI1), .U(U[6]), .VEM_1(_5VAI1), .A(A[6]), .B(B[6]), .in_4(in_3));
  ULA_1_BIT ula_1_bit_11 (.VAI_1(_16VAI1), .U(U[16]), .VEM_1(_15VAI1), .A(A[16]), .B(B[16]), .in_4(in_3));
  ULA_1_BIT ula_1_bit_12 (.VAI_1(_26VAI1), .U(U[26]), .VEM_1(_25VAI1), .A(A[26]), .B(B[26]), .in_4(in_3));
  ULA_1_BIT ula_1_bit_13 (.VAI_1(_5VAI1), .U(U[5]), .VEM_1(_4VAI1), .A(A[5]), .B(B[5]), .in_4(in_3));
  ULA_1_BIT ula_1_bit_14 (.VAI_1(_15VAI1), .U(U[15]), .VEM_1(_14VAI1), .A(A[15]), .B(B[15]), .in_4(in_3));
  ULA_1_BIT ula_1_bit_15 (.VAI_1(_25VAI1), .U(U[25]), .VEM_1(_24VAI1), .A(A[25]), .B(B[25]), .in_4(in_3));
  ULA_1_BIT ula_1_bit_16 (.VAI_1(_4VAI1), .U(U[4]), .VEM_1(_3VAI1), .A(A[4]), .B(B[4]), .in_4(in_3));
  ULA_1_BIT ula_1_bit_17 (.VAI_1(_14VAI1), .U(U[14]), .VEM_1(_13VAI1), .A(A[14]), .B(B[14]), .in_4(in_3));
  ULA_1_BIT ula_1_bit_18 (.VAI_1(_24VAI1), .U(U[24]), .VEM_1(_23VAI1), .A(A[24]), .B(B[24]), .in_4(in_3));
  ULA_1_BIT ula_1_bit_19 (.VAI_1(_3VAI1), .U(U[3]), .VEM_1(_2VAI1), .A(A[3]), .B(B[3]), .in_4(in_3));
  ULA_1_BIT ula_1_bit_20 (.VAI_1(_13VAI1), .U(U[13]), .VEM_1(_12VAI1), .A(A[13]), .B(B[13]), .in_4(in_3));
  ULA_1_BIT ula_1_bit_21 (.VAI_1(_23VAI1), .U(U[23]), .VEM_1(_22VAI1), .A(A[23]), .B(B[23]), .in_4(in_3));
  ULA_1_BIT ula_1_bit_22 (.VAI_1(_2VAI1), .U(U[2]), .VEM_1(_1VAI1), .A(A[2]), .B(B[2]), .in_4(in_3));
  ULA_1_BIT ula_1_bit_23 (.VAI_1(_12VAI1), .U(U[12]), .VEM_1(_11VAI1), .A(A[12]), .B(B[12]), .in_4(in_3));
  ULA_1_BIT ula_1_bit_24 (.VAI_1(_22VAI1), .U(U[22]), .VEM_1(_21VAI1), .A(A[22]), .B(B[22]), .in_4(in_3));
  ULA_1_BIT ula_1_bit_25 (.VAI_1(_1VAI1), .U(U[1]), .VEM_1(_0VAI1), .A(A[1]), .B(B[1]), .in_4(in_3));
  ULA_1_BIT ula_1_bit_26 (.VAI_1(_11VAI1), .U(U[11]), .VEM_1(_10VAI1), .A(A[11]), .B(B[11]), .in_4(in_3));
  ULA_1_BIT ula_1_bit_27 (.VAI_1(_21VAI1), .U(U[21]), .VEM_1(_20VAI1), .A(A[21]), .B(B[21]), .in_4(in_3));
  ULA_1_BIT ula_1_bit_28 (.VAI_1(OVERFLOW), .U(U[31]), .VEM_1(_30VAI1), .A(A[31]), .B(B[31]), .in_4(in_3));
  ULA_1_BIT ula_1_bit_29 (.VAI_1(_30VAI1), .U(U[30]), .VEM_1(_29VAI1), .A(A[30]), .B(B[30]), .in_4(in_3));
  ULA_1_BIT ula_1_bit_30 (.VAI_1(_0VAI1), .U(U[0]), .VEM_1(1'b0), .A(A[0]), .B(B[0]), .in_4(in_3));
  ULA_1_BIT ula_1_bit_31 (.VAI_1(_10VAI1), .U(U[10]), .VEM_1(_9VAI1), .A(A[10]), .B(B[10]), .in_4(in_3));
  ULA_1_BIT ula_1_bit_32 (.VAI_1(_20VAI1), .U(U[20]), .VEM_1(_19VAI1), .A(A[20]), .B(B[20]), .in_4(in_3));

  // Other names for the same wires on the sheet: _31VAI1 = OVERFLOW

  // Notes on the sheet:
  //   00000 -> AND
  //   00001 -> OR
  //   00010 -> XOR
  //   00011 -> SOMA
endmodule

module mux32 (
  input  P,
  input  O,
  input  N,
  input  M,
  input  L,
  input  K,
  input  J,
  input  I,
  input  H,
  input  G,
  input  F,
  input  E,
  input  D,
  input  C,
  input  B,
  input  A,
  input  Z6,
  input  Z5,
  input  Z4,
  input  Z3,
  input  Z2,
  input  Z1,
  input  Z,
  input  Y,
  input  X,
  input  W,
  input  V,
  input  U,
  input  T,
  input  S,
  input  R,
  input  Q,
  input  SEL_4,
  input  SEL_3,
  input  SEL_2,
  input  SEL_1,
  input  SEL_0,
  output out_38
);

  wire mux16_1_out_21, mux16_2_out_21;

  mux16 mux16_1 (
    .out_21(mux16_1_out_21), .Canal_0(A), .Canal_1(B), .Canal_2(C), .Canal_3(D), .Canal_4(E), .Canal_5(F),
    .Canal_6(G), .Canal_7(H), .Canal_8(I), .Canal_9(J), .Canal_10(K), .Canal_11(L), .Canal_12(M),
    .Canal_13(N), .Canal_14(O), .Canal_15(P), .SEL_0(SEL_0), .SEL_1(SEL_1), .SEL_2(SEL_2), .SEL_3(SEL_3));
  mux16 mux16_2 (
    .out_21(mux16_2_out_21), .Canal_0(Q), .Canal_1(R), .Canal_2(S), .Canal_3(T), .Canal_4(U), .Canal_5(V),
    .Canal_6(W), .Canal_7(X), .Canal_8(Y), .Canal_9(Z), .Canal_10(Z1), .Canal_11(Z2), .Canal_12(Z3),
    .Canal_13(Z4), .Canal_14(Z5), .Canal_15(Z6), .SEL_0(SEL_0), .SEL_1(SEL_1), .SEL_2(SEL_2), .SEL_3(SEL_3));
  mux2 mux2_1 (.Canal_0(mux16_1_out_21), .Canal_1(mux16_2_out_21), .out_4(out_38), .Seletor_0(SEL_4));
endmodule
